// Logisim project TTL-Computer.circ as structural Verilog: 12 circuits, main circuit 74xx-Computer
module _74xx_Computer (
  input  [7:0] DATA_BUS__IN,
  input  MEM_BOOT_ROM,
  input  MEM_PROGRAM_RAM,
  input  [7:0] MANUAL_DATA,
  output [7:0] DATA_BUS__OUT,
  output Fgt,
  output Feq,
  output Flt,
  output Fz,
  output Fc
);

  wire ALU_Cn, ALU_M, ALU_S0, ALU_S1, ALU_S2, ALU_S3, and_1_out, CLOCK_64X, clock_divider_1_clock_div8,
       CLOCK_HALT, nA_DATA_LOAD, nA_DATA_OUT, nALU_A_IN, nALU_B_IN, nALU_OUT, nB_DATA_LOAD, nB_DATA_OUT,
       nC_DATA_LOAD, nC_DATA_OUT, nD_DATA_LOAD, nD_DATA_OUT, nFLAGS_LOAD, nIR_LOAD, nMAR_HB_LOAD,
       nMAR_LB_LOAD, nMAR_PC_LOAD, nMAR_STK_LOAD, nMEM_OUT, nMEM_RAM_LOAD, not_1_out, nPC_H_LOAD, nPC_H_OUT,
       nPC_L_LOAD, nPC_L_OUT, nSTK_RESET, PC_DEC, PC_INC, STK_DEC, STK_INC;
  wire [3:0] ALU_contents_bus_out, ALU_contents_bus_out_2, Memory_Access_Register_data_out,
       Memory_Access_Register_data_out_2, Memory_Access_Register_data_out_3,
       Memory_Access_Register_data_out_4, Memory_contents_out, Memory_contents_out_2,
       Program_Counter_mar_bus_out, Program_Counter_mar_bus_out_2, Program_Counter_mar_bus_out_3,
       Program_Counter_mar_bus_out_4, Register_A_contents_bus_out, Register_A_contents_bus_out_2,
       Register_B_contents_bus_out, Register_B_contents_bus_out_2, Register_C_contents_bus_out,
       Register_C_contents_bus_out_2, Register_D_contents_bus_out, Register_D_contents_bus_out_2;
  wire [4:0] ALU_fc;
  wire [6:0] Instruction_Register_contents_bus_out;
  wire [7:0] Flags_Register_data_bus_out;
  wire [7:5] Flags_Register_contents_bus_out;
  wire [7:7] Instruction_Register_contents_bus_out_2;
  wire [15:0] Stack_Pointer_mar_bus_out;

  Clock clock_1 (.out(CLOCK_64X));
  Hex_Digit_Display hex_digit_display_1 (.value(DATA_BUS__IN[7:4]));  // open: dp
  Hex_Digit_Display hex_digit_display_2 (.value(DATA_BUS__IN[3:0]));  // open: dp
  Hex_Digit_Display hex_digit_display_3 (.value(Program_Counter_mar_bus_out_4));  // open: dp
  Hex_Digit_Display hex_digit_display_4 (.value(Program_Counter_mar_bus_out_3));  // open: dp
  not not_1 (not_1_out, CLOCK_HALT);
  Clock_Divider clock_divider_1 (.CLOCK(CLOCK_64X), .CLOCK_DIV8(clock_divider_1_clock_div8));  // open: CLOCK_DIV64
  Hex_Digit_Display hex_digit_display_5 (.value(Register_C_contents_bus_out));  // open: dp
  Hex_Digit_Display hex_digit_display_6 (.value(Register_C_contents_bus_out_2));  // open: dp
  Register Register_C (
    .CLOCK(and_1_out), .nDATA_OUT(nC_DATA_OUT), .nDATA_LOAD(nC_DATA_LOAD),
    .CONTENTS_BUS_OUT({Register_C_contents_bus_out_2, Register_C_contents_bus_out}),
    .DATA_BUS_OUT(DATA_BUS__IN), .DATA_BUS_IN(DATA_BUS__IN));
  Hex_Digit_Display hex_digit_display_7 (.value(Program_Counter_mar_bus_out_2));  // open: dp
  Hex_Digit_Display hex_digit_display_8 (.value(Program_Counter_mar_bus_out));  // open: dp
  Hex_Digit_Display hex_digit_display_9 (.value(Register_D_contents_bus_out_2));  // open: dp
  Hex_Digit_Display hex_digit_display_10 (.value(Register_D_contents_bus_out));  // open: dp
  Register Register_D (
    .CLOCK(and_1_out), .nDATA_OUT(nD_DATA_OUT), .nDATA_LOAD(nD_DATA_LOAD),
    .CONTENTS_BUS_OUT({Register_D_contents_bus_out_2, Register_D_contents_bus_out}),
    .DATA_BUS_OUT(DATA_BUS__IN), .DATA_BUS_IN(DATA_BUS__IN));
  Hex_Digit_Display hex_digit_display_11 (.value(Register_A_contents_bus_out_2));  // open: dp
  Hex_Digit_Display hex_digit_display_12 (.value(Register_A_contents_bus_out));  // open: dp
  Register Register_A (
    .CLOCK(and_1_out), .nDATA_OUT(nA_DATA_OUT), .nDATA_LOAD(nA_DATA_LOAD),
    .CONTENTS_BUS_OUT({Register_A_contents_bus_out_2, Register_A_contents_bus_out}),
    .DATA_BUS_OUT(DATA_BUS__IN), .DATA_BUS_IN(DATA_BUS__IN));
  Hex_Digit_Display hex_digit_display_13 (.value(Register_B_contents_bus_out));  // open: dp
  Hex_Digit_Display hex_digit_display_14 (.value(Register_B_contents_bus_out_2));  // open: dp
  Register Register_B (
    .CLOCK(and_1_out), .nDATA_OUT(nB_DATA_OUT), .nDATA_LOAD(nB_DATA_LOAD),
    .CONTENTS_BUS_OUT({Register_B_contents_bus_out_2, Register_B_contents_bus_out}),
    .DATA_BUS_OUT(DATA_BUS__IN), .DATA_BUS_IN(DATA_BUS__IN));
  and and_1 (and_1_out, not_1_out, clock_divider_1_clock_div8);
  Program_Counter Program_Counter (
    .PC_INC(PC_INC), .PC_DEC(PC_DEC), .CLOCK(and_1_out), .PC_L_DATA_IN(DATA_BUS__IN),
    .nPC_L_LOAD(nPC_L_LOAD), .PC_H_DATA_IN(DATA_BUS__IN), .nPC_H_LOAD(nPC_H_LOAD),
    .MAR_BUS_OUT({Program_Counter_mar_bus_out_4, Program_Counter_mar_bus_out_3, Program_Counter_mar_bus_out_2, Program_Counter_mar_bus_out}),
    .nPC_L_OUT(nPC_L_OUT), .PC_L_DATA_OUT(DATA_BUS__IN), .PC_H_DATA_OUT(DATA_BUS__IN), .nPC_H_OUT(nPC_H_OUT));
  Register Flags_Register (
    .CLOCK(and_1_out), .nDATA_OUT(1'b0), .nDATA_LOAD(nFLAGS_LOAD),
    .CONTENTS_BUS_OUT({Flags_Register_contents_bus_out, Fgt, Feq, Flt, Fz, Fc}),
    .DATA_BUS_OUT(Flags_Register_data_bus_out), .DATA_BUS_IN({3'b000, ALU_fc}));
  Hex_Digit_Display hex_digit_display_15 (.value(Stack_Pointer_mar_bus_out[15:12]));  // open: dp
  Stack_Pointer Stack_Pointer (
    .STK_DEC(STK_DEC), .CLOCK(and_1_out), .nSTK_RESET(nSTK_RESET), .MAR_BUS_OUT(Stack_Pointer_mar_bus_out),
    .STK_INC(STK_INC));
  Hex_Digit_Display hex_digit_display_16 (.value(Memory_Access_Register_data_out_4));  // open: dp
  Memory_Access_Register Memory_Access_Register (
    .LB_DATA_IN(DATA_BUS__IN), .CLOCK(and_1_out), .nLB_LOAD(nMAR_LB_LOAD), .HB_DATA_IN(DATA_BUS__IN),
    .nHB_LOAD(nMAR_HB_LOAD),
    .PC_DATA_IN({Program_Counter_mar_bus_out_4, Program_Counter_mar_bus_out_3, Program_Counter_mar_bus_out_2, Program_Counter_mar_bus_out}),
    .STK_DATA_IN(Stack_Pointer_mar_bus_out), .nPC_LOAD(nMAR_PC_LOAD), .nSTK_LOAD(nMAR_STK_LOAD),
    .DATA_OUT({Memory_Access_Register_data_out_4, Memory_Access_Register_data_out_3, Memory_Access_Register_data_out_2, Memory_Access_Register_data_out}));
  ALU ALU (
    .DATA_BUS_IN(DATA_BUS__IN), .CLOCK(and_1_out), .nA_IN(nALU_A_IN), .nB_IN(nALU_B_IN), .S3(ALU_S3),
    .S2(ALU_S2), .S1(ALU_S1), .S0(ALU_S0), .M(ALU_M), .Cn(ALU_Cn), .nALU_OUT(nALU_OUT), .Flt(ALU_fc[2]),
    .Feq(ALU_fc[3]), .Fgt(ALU_fc[4]), .DATA_BUS_OUT(DATA_BUS__IN), .Fc(ALU_fc[0]),
    .CONTENTS_BUS_OUT({ALU_contents_bus_out_2, ALU_contents_bus_out}), .Fz(ALU_fc[1]));
  Hex_Digit_Display hex_digit_display_17 (.value(Stack_Pointer_mar_bus_out[7:4]));  // open: dp
  Hex_Digit_Display hex_digit_display_18 (.value(Stack_Pointer_mar_bus_out[11:8]));  // open: dp
  Hex_Digit_Display hex_digit_display_19 (.value(Memory_Access_Register_data_out_3));  // open: dp
  Hex_Digit_Display hex_digit_display_20 (.value(Memory_Access_Register_data_out_2));  // open: dp
  Hex_Digit_Display hex_digit_display_21 (.value(ALU_contents_bus_out));  // open: dp
  Hex_Digit_Display hex_digit_display_22 (.value(ALU_contents_bus_out_2));  // open: dp
  Hex_Digit_Display hex_digit_display_23 (.value(Stack_Pointer_mar_bus_out[3:0]));  // open: dp
  Hex_Digit_Display hex_digit_display_24 (.value(Memory_Access_Register_data_out));  // open: dp
  DotMatrix #(.matrixcols(7), .matrixrows(1), .dotshape("circle")) dotmatrix_1 (
    .col0(Instruction_Register_contents_bus_out[6]), .col1(Instruction_Register_contents_bus_out[5]),
    .col2(Instruction_Register_contents_bus_out[4]), .col3(Instruction_Register_contents_bus_out[3]),
    .col4(Instruction_Register_contents_bus_out[2]), .col5(Instruction_Register_contents_bus_out[1]),
    .col6(Instruction_Register_contents_bus_out[0]));
  Hex_Digit_Display hex_digit_display_25 (.value({Instruction_Register_contents_bus_out_2[7], Instruction_Register_contents_bus_out[6:4]}));  // open: dp
  Hex_Digit_Display hex_digit_display_26 (.value(Instruction_Register_contents_bus_out[3:0]));  // open: dp
  Register Instruction_Register (
    .CLOCK(and_1_out), .nDATA_OUT(1'b0), .nDATA_LOAD(nIR_LOAD),
    .CONTENTS_BUS_OUT({Instruction_Register_contents_bus_out_2[7], Instruction_Register_contents_bus_out}),
    .DATA_BUS_IN(DATA_BUS__IN));  // open: DATA_BUS_OUT
  Sequencer_Instruction_Decoder Instruction_Decoder (
    .FLAGS_DATA_IN(Flags_Register_data_bus_out[4:0]),
    .INSTRUCTION_DATA_IN(Instruction_Register_contents_bus_out), .CLOCK_64X(CLOCK_64X),
    .nA_DATA_OUT(nA_DATA_OUT), .nA_DATA_LOAD(nA_DATA_LOAD), .nB_DATA_OUT(nB_DATA_OUT),
    .nB_DATA_LOAD(nB_DATA_LOAD), .nC_DATA_OUT(nC_DATA_OUT), .nC_DATA_LOAD(nC_DATA_LOAD),
    .nD_DATA_OUT(nD_DATA_OUT), .nD_DATA_LOAD(nD_DATA_LOAD), .nFLAGS_LOAD(nFLAGS_LOAD), .nIR_LOAD(nIR_LOAD),
    .PC_INC(PC_INC), .PC_DEC(PC_DEC), .nPC_L_LOAD(nPC_L_LOAD), .nPC_H_LOAD(nPC_H_LOAD),
    .nPC_L_OUT(nPC_L_OUT), .nPC_H_OUT(nPC_H_OUT), .STK_INC(STK_INC), .STK_DEC(STK_DEC),
    .nSTK_RESET(nSTK_RESET), .nALU_A_IN(nALU_A_IN), .nALU_B_IN(nALU_B_IN), .ALU_S0(ALU_S0), .ALU_S1(ALU_S1),
    .ALU_S2(ALU_S2), .ALU_S3(ALU_S3), .ALU_M(ALU_M), .ALU_Cn(ALU_Cn), .nALU_OUT(nALU_OUT),
    .nMAR_LB_LOAD(nMAR_LB_LOAD), .nMAR_HB_LOAD(nMAR_HB_LOAD), .nMAR_PC_LOAD(nMAR_PC_LOAD),
    .nMAR_STK_LOAD(nMAR_STK_LOAD), .nMEM_RAM_LOAD(nMEM_RAM_LOAD), .nMEM_OUT(nMEM_OUT),
    .CLOCK_HALT(CLOCK_HALT), .CLOCK(and_1_out));  // open: LOAD
  Hex_Digit_Display hex_digit_display_27 (.value(Memory_contents_out_2));  // open: dp
  Memory Memory (
    .BOOT_ROM(MEM_BOOT_ROM), .PROGRAM_RAM(MEM_PROGRAM_RAM), .nRAM_LOAD(nMEM_RAM_LOAD), .nMEM_OUT(nMEM_OUT),
    .CLOCK(and_1_out), .DATA_IN(DATA_BUS__IN), .MANUAL_DATA_IN(MANUAL_DATA), .DATA_OUT(DATA_BUS__IN),
    .ADDRESS_IN({Memory_Access_Register_data_out_4, Memory_Access_Register_data_out_3, Memory_Access_Register_data_out_2, Memory_Access_Register_data_out}),
    .CONTENTS_OUT({Memory_contents_out_2, Memory_contents_out}));
  Hex_Digit_Display hex_digit_display_28 (.value(Memory_contents_out));  // open: dp

  assign DATA_BUS__OUT = DATA_BUS__IN;

  // Notes on the sheet:
  //   Create separate input selector per flag?
  //   ~FLAGS_OUT
endmodule

module Controller (
  input  [4:0] FLAGS_DATA_IN,
  input  [6:0] INSTRUCTION_DATA_IN,
  input  CLOCK,
  input  CLOCK_64X,
  input  LOAD,
  output nA_DATA_OUT,
  output nSTK_RESET,
  output nA_DATA_LOAD,
  output nALU_A_IN,
  output nB_DATA_OUT,
  output nALU_B_IN,
  output nB_DATA_LOAD,
  output ALU_S0,
  output nC_DATA_OUT,
  output ALU_S1,
  output nC_DATA_LOAD,
  output ALU_S2,
  output nD_DATA_OUT,
  output ALU_S3,
  output nD_DATA_LOAD,
  output ALU_M,
  output nFLAGS_LOAD,
  output ALU_Cn,
  output nIR_LOAD,
  output nALU_OUT,
  output nMAR_LB_LOAD,
  output PC_INC,
  output nMAR_HB_LOAD,
  output nMAR_PC_LOAD,
  output PC_DEC,
  output nMAR_STK_LOAD,
  output nPC_L_LOAD,
  output nMEM_RAM_LOAD,
  output nPC_H_LOAD,
  output nMEM_OUT,
  output nPC_L_OUT,
  output nPC_H_OUT,
  output CLOCK_HALT,
  output STK_INC,
  output STK_DEC
);

  wire A_DATA_LOAD, A_DATA_OUT, ALU_A_IN, ALU_B_IN, ALU_OUT, and_3_out, and_4_out, and_6_out, and_7_out,
       B_DATA_LOAD, B_DATA_OUT, C_DATA_LOAD, C_DATA_OUT, CLOCK_64X_t, CLOCK_t, D_DATA_LOAD, D_DATA_OUT,
       dip_7474_1_p2, dip_74161_1_p1, dip_74161_1_p2, dip_74161_1_p9, dip_74161_1_p13, dip_74161_1_p14,
       dip_74161_1_p15, dip_74161_2_p1, dip_74161_2_p2, dip_74161_2_p4, dip_74161_2_p6, dip_74161_2_p8,
       dip_74161_2_p10, dip_74161_2_p14, dip_74161_2_p16, dip_74595_1_p2, dip_74595_1_p6, dip_74595_1_p10,
       dip_74595_2_p6, dip_74595_3_p6, dip_74595_4_p6, dip_74595_5_p6, dip_74595_6_p7, DONE, FLAGS_LOAD,
       IN_OUT, IR_LOAD, LOAD_t, MAR_HB_LOAD, MAR_LB_LOAD, MAR_PC_LOAD, MAR_STK_LOAD, MEM_OUT, MEM_RAM_LOAD,
       nor_2_out, nor_3_out, not_25_out, not_29_out, not_30_out, not_31_out, not_32_out, not_35_out,
       not_36_out, or_1_out, or_3_out, or_4_out, or_5_out, or_6_out, OUT1_IN, OUT2_IN, PC_H_LOAD, PC_H_OUT,
       PC_INC_t, PC_L_LOAD, PC_L_OUT, STK_RESET, TSTATE_0, TSTATE_1, TSTATE_RESET;
  wire [2:0] BANK;
  wire [3:0] T_STATE, undriven, undriven_2;
  wire [3:3] undriven_3;
  wire [7:0] dip_74595_1_p12, dip_74595_2_p8, dip_74595_3_p8, dip_74595_4_p8, dip_74595_5_p8, dip_74595_6_p9,
       rom_1_data;

  not not_1 (nA_DATA_OUT, A_DATA_OUT);
  not not_2 (nA_DATA_LOAD, A_DATA_LOAD);
  not not_3 (nB_DATA_OUT, B_DATA_OUT);
  not not_4 (nB_DATA_LOAD, B_DATA_LOAD);
  not not_5 (nC_DATA_OUT, C_DATA_OUT);
  not not_6 (nC_DATA_LOAD, C_DATA_LOAD);
  not not_7 (nD_DATA_OUT, D_DATA_OUT);
  not not_8 (nD_DATA_LOAD, D_DATA_LOAD);
  not not_9 (nFLAGS_LOAD, FLAGS_LOAD);
  not not_10 (nIR_LOAD, or_1_out);
  not not_11 (nPC_L_LOAD, PC_L_LOAD);
  not not_12 (nPC_H_LOAD, PC_H_LOAD);
  not not_13 (nPC_L_OUT, PC_L_OUT);
  not not_14 (nPC_H_OUT, PC_H_OUT);
  // Probe on FLAGS_DATA_IN[3]
  // Probe on FLAGS_DATA_IN[4]
  Clock_Divider clock_divider_1 (.CLOCK(CLOCK_64X_t), .CLOCK_DIV8(CLOCK_t));  // open: CLOCK_DIV64
  Clock u_CLOCK_64X (.out(CLOCK_64X_t));
  or or_1 (or_1_out, IR_LOAD, TSTATE_1);
  or or_2 (PC_INC, PC_INC_t, TSTATE_1);
  // Probe on FLAGS_DATA_IN[2]
  // Probe on FLAGS_DATA_IN[1]
  // Probe on FLAGS_DATA_IN[0]
  // Probe on INSTRUCTION_DATA_IN[6]
  // Probe on INSTRUCTION_DATA_IN[5]
  // Probe on INSTRUCTION_DATA_IN[3]
  // Probe on INSTRUCTION_DATA_IN[2]
  // Probe on INSTRUCTION_DATA_IN[4]
  not not_15 (nSTK_RESET, STK_RESET);
  not not_16 (nALU_A_IN, ALU_A_IN);
  not not_17 (nALU_B_IN, ALU_B_IN);
  not not_18 (nALU_OUT, ALU_OUT);
  not not_19 (nMAR_LB_LOAD, MAR_LB_LOAD);
  not not_20 (nMAR_HB_LOAD, MAR_HB_LOAD);
  not not_21 (nMAR_PC_LOAD, or_3_out);
  not not_22 (nMAR_STK_LOAD, MAR_STK_LOAD);
  not not_23 (nMEM_RAM_LOAD, MEM_RAM_LOAD);
  not not_24 (nMEM_OUT, or_4_out);
  // Probe on INSTRUCTION_DATA_IN[1]
  // Probe on INSTRUCTION_DATA_IN[0]
  or or_3 (or_3_out, MAR_PC_LOAD, TSTATE_0);
  or or_4 (or_4_out, MEM_OUT, TSTATE_1);
  // Probe on T_STATE[1]
  // Probe on T_STATE[3]
  // Probe on T_STATE[2]
  // Probe on T_STATE[0]
  DotMatrix #(.matrixcols(4), .matrixrows(1), .dotshape("circle")) dotmatrix_1 (
    .col0(T_STATE[2]), .col1(T_STATE[3]), .col2(T_STATE[1]), .col3(T_STATE[0]));
  _74161_Clockfix u_74161_clockfix_1 (
    .CLK(CLOCK_t), .CLR(not_25_out), .LE(1'b1), .CEP(1'b1), .CET(1'b1), .D1(1'b0), .D2(1'b0), .D3(1'b0),
    .D4(1'b0), .Q1(T_STATE[0]), .Q2(T_STATE[1]), .Q3(T_STATE[3]), .Q4(T_STATE[2]));  // open: TC
  not not_25 (not_25_out, TSTATE_RESET);
  // DIP_74161 dip_74161_1: pin names not known; wires that end beside it: dip_74161_1_p1, dip_74161_1_p2, BANK[0], 1'b0, BANK[1], 1'b0, BANK[2], 1'b0, dip_74161_1_p9, 1'b0, 1'b1, 1'b1, dip_74161_1_p13, dip_74161_1_p14, dip_74161_1_p15
  not not_26 (dip_74161_1_p2, dip_74161_1_p1);
  DotMatrix #(.matrixcols(4), .matrixrows(1), .dotshape("circle")) dotmatrix_2 (
    .col0(dip_74161_1_p9), .col1(BANK[2]), .col2(BANK[1]), .col3(BANK[0]));
  nor nor_1 (TSTATE_0, T_STATE[0], T_STATE[1], T_STATE[2], T_STATE[3]);
  and and_1 (TSTATE_1, T_STATE[0], nor_2_out);
  nor nor_2 (nor_2_out, T_STATE[1], T_STATE[2], T_STATE[3]);
  and and_2 (dip_74161_1_p15, BANK[1], BANK[2]);
  not not_27 (dip_74161_1_p13, 1'b0);
  ROM #(.addrWidth(19)) rom_1 (
    .addr({FLAGS_DATA_IN, INSTRUCTION_DATA_IN, T_STATE, BANK}), .data(rom_1_data), .sel(1'b1));
  nor nor_3 (nor_3_out, LOAD_t, and_4_out);
  not not_28 (LOAD_t, CLOCK_t);
  and and_3 (and_3_out, DONE, not_29_out);
  not not_29 (not_29_out, CLOCK_64X_t);
  // IC_74377 ic_74377_1: pin names not known
  not not_30 (not_30_out, and_3_out);
  Hex_Digit_Display hex_digit_display_1 (.value(undriven_2));  // open: dp
  Hex_Digit_Display hex_digit_display_2 (.value(undriven));  // open: dp
  // IC_74377 ic_74377_2: pin names not known; wires that end beside it: and_3_out, not_30_out
  // DIP_74595 dip_74595_1: pin names not known; wires that end beside it: dip_74595_1_p12[7], dip_74595_1_p2, dip_74595_1_p12[6], dip_74161_1_p14, dip_74595_1_p12[5], dip_74595_1_p6, dip_74595_1_p12[4], 1'b0, dip_74595_1_p12[3], dip_74595_1_p10, dip_74595_1_p12[2], dip_74595_1_p12[0], dip_74595_1_p12[1], dip_74595_1_p10, dip_74595_2_p8[7], dip_74595_1_p2, dip_74595_2_p8[6], dip_74161_1_p14
  Hex_Digit_Display hex_digit_display_3 (.value({TSTATE_RESET, CLOCK_HALT, MEM_OUT, MEM_RAM_LOAD}));  // open: dp
  Hex_Digit_Display hex_digit_display_4 (.value({undriven_3[3], OUT2_IN, OUT1_IN, IN_OUT}));  // open: dp
  // IC_74377 ic_74377_3: pin names not known
  // DIP_74595 dip_74595_2: pin names not known; wires that end beside it: dip_74595_2_p8[5], dip_74595_1_p6, dip_74595_2_p8[4], 1'b0, dip_74595_2_p8[3], dip_74595_2_p6, dip_74595_2_p8[2], dip_74595_2_p8[0], dip_74595_2_p8[1], dip_74595_2_p6, dip_74595_3_p8[7], dip_74595_1_p2, dip_74595_3_p8[6], dip_74161_1_p14
  Hex_Digit_Display hex_digit_display_5 (.value({MAR_STK_LOAD, MAR_PC_LOAD, MAR_HB_LOAD, MAR_LB_LOAD}));  // open: dp
  Hex_Digit_Display hex_digit_display_6 (.value({ALU_OUT, ALU_Cn, ALU_M, ALU_S3}));  // open: dp
  // IC_74377 ic_74377_4: pin names not known; wires that end beside it: and_3_out, not_30_out, and_3_out, not_30_out
  // DIP_74595 dip_74595_3: pin names not known; wires that end beside it: dip_74595_3_p8[5], dip_74595_1_p6, dip_74595_3_p8[4], 1'b0, dip_74595_3_p8[3], dip_74595_3_p6, dip_74595_3_p8[2], dip_74595_3_p8[0], dip_74595_3_p8[1], dip_74595_3_p6, dip_74595_4_p8[7], dip_74595_1_p2, dip_74595_4_p8[6], dip_74161_1_p14
  and and_4 (and_4_out, and_7_out, CLOCK_64X_t);
  Hex_Digit_Display hex_digit_display_7 (.value({ALU_S2, ALU_S1, ALU_S0, ALU_B_IN}));  // open: dp
  Hex_Digit_Display hex_digit_display_8 (.value({ALU_A_IN, STK_RESET, STK_DEC, STK_INC}));  // open: dp
  // IC_74377 ic_74377_5: pin names not known
  // DIP_74595 dip_74595_4: pin names not known; wires that end beside it: dip_74595_4_p8[5], dip_74595_1_p6, dip_74595_4_p8[4], 1'b0, dip_74595_4_p8[3], dip_74595_4_p6, dip_74595_4_p8[2], dip_74595_4_p8[0], dip_74595_4_p8[1], dip_74595_4_p6, dip_74595_5_p8[7], dip_74595_1_p2, dip_74595_5_p8[6], dip_74161_1_p14
  nor nor_4 (dip_74595_1_p2, nor_3_out, or_5_out);
  or or_5 (or_5_out, and_7_out, not_31_out);
  not not_31 (not_31_out, CLOCK_64X_t);
  Hex_Digit_Display hex_digit_display_9 (.value({PC_H_OUT, PC_L_OUT, PC_H_LOAD, PC_L_LOAD}));  // open: dp
  Hex_Digit_Display hex_digit_display_10 (.value({PC_DEC, PC_INC_t, IR_LOAD, FLAGS_LOAD}));  // open: dp
  // IC_74377 ic_74377_6: pin names not known; wires that end beside it: and_3_out, not_30_out, and_3_out, not_30_out, and_3_out
  // DIP_74595 dip_74595_5: pin names not known; wires that end beside it: dip_74595_5_p8[5], dip_74595_1_p6, dip_74595_5_p8[4], 1'b0, dip_74595_5_p8[3], dip_74595_5_p6, dip_74595_5_p8[2], dip_74595_5_p8[0], dip_74595_5_p8[1], dip_74595_5_p6, dip_74595_6_p9[7], dip_74595_1_p2, dip_74595_6_p9[6], dip_74161_1_p14
  and and_5 (dip_74161_1_p14, and_6_out, not_32_out);
  and and_6 (and_6_out, or_6_out, CLOCK_64X_t);
  not not_32 (not_32_out, DONE);
  or or_6 (or_6_out, nor_3_out, and_7_out);
  Hex_Digit_Display hex_digit_display_11 (.value({B_DATA_LOAD, B_DATA_OUT, A_DATA_LOAD, A_DATA_OUT}));  // open: dp
  Hex_Digit_Display hex_digit_display_12 (.value({D_DATA_LOAD, D_DATA_OUT, C_DATA_LOAD, C_DATA_OUT}));  // open: dp
  // DIP_74595 dip_74595_6: pin names not known; wires that end beside it: dip_74595_6_p9[5], dip_74595_1_p6, not_30_out, dip_74595_6_p9[4], 1'b0, dip_74595_6_p9[3], dip_74595_6_p7, dip_74595_6_p9[2], dip_74595_6_p9[0], dip_74595_6_p9[1], dip_74595_6_p7
  not not_33 (dip_74595_1_p6, dip_74161_1_p14);
  and and_7 (and_7_out, dip_74161_2_p4, dip_74161_2_p6, dip_74161_2_p8);
  DotMatrix #(.matrixcols(4), .matrixrows(1), .dotshape("circle")) dotmatrix_3 (
    .col0(dip_74161_2_p10), .col1(dip_74161_2_p8), .col2(dip_74161_2_p6), .col3(dip_74161_2_p4));
  // DIP_74161 dip_74161_2: pin names not known; wires that end beside it: dip_74161_2_p1, dip_74161_2_p2, dip_74161_1_p14, dip_74161_2_p4, 1'b0, dip_74161_2_p6, 1'b0, dip_74161_2_p8, 1'b0, dip_74161_2_p10, 1'b0, 1'b1, 1'b1, dip_74161_2_p14, dip_74595_1_p2, dip_74161_2_p16
  or or_7 (dip_74161_2_p2, and_7_out, dip_74161_2_p1);
  not not_34 (dip_74161_2_p14, and_7_out);
  // AND_Gate and_8 has open pins: in1=dip_74161_1_p14, out=open
  not not_35 (not_35_out, and_7_out);
  not not_36 (not_36_out, CLOCK_64X_t);
  nor nor_5 (dip_74161_2_p16, not_35_out, dip_74161_1_p14, not_36_out);
  // NOT_Gate not_37 is placed but not wired
  // DIP_7474 dip_7474_1: pin names not known; wires that end beside it: CLOCK_t, dip_7474_1_p2, dip_7474_1_p2, DONE

  // Other names for the same wires on the sheet: INSTRUCTION[6:0] = INSTRUCTION_DATA_IN; FLAGS[4:0] = FLAGS_DATA_IN

  // Notes on the sheet:
  //   LOAD: pull=down
  //   T-STATE COUNTER
  //   CLR
  //   DATA BYTE COUNTER
  //   CE
  //   CONTROL ROM
  //   RESTART
  //   ROM DATA
  //   contents of rom_1 (hex, n*v repeats v):
  //   17*0 8 127*0 4 131*0 9 0 0 0 8 123*0 21 0 0 0 8 123*0 81 0 0 0 8 123*0 6 0 0 0 8 123*0 24 0 0 0 8
  //   123*0 84 0 0 0 8 123*0 12 0 0 0 8 123*0 18 0 0 0 8 123*0 90 0 0 0 8 123*0 42 0 0 0 8 123*0 48 0 0 0
  //   8 123*0 60 0 0 0 8 120*0 40 6*0 2 0 0 4 2 0 0 0 8 112*0 40 6*0 2 0 0 4 8 0 0 0 8 112*0 40 6*0 2 0 0
  //   4 20 0 0 0 8 112*0 40 6*0 2 0 0 4 80 0 0 0 8 112*0 40 6*0 2 0 0 4 80 4*0 40 6*0 2 0 0 4 20 4*0 10 0
  //   0 10 4*0 20 0 0 40 0 0 0 a 0 0 0 2 76*0 40 6*0 2 0 0 4 80 4*0 40 6*0 2 0 0 4 20 4*0 10 0 0 10 4*0 20
  //   0 0 40 0 0 0 a 0 0 0 8 332*0 40 6*0 2 0 0 4 80 4*0 40 6*0 2 0 0 4 20 4*0 10 0 0 10 4*0 20 0 0 40 0 0
  //   0 9 0 0 0 1 76*0 40 6*0 2 0 0 4 80 4*0 40 6*0 2 0 0 4 20 4*0 10 0 0 10 4*0 20 0 0 40 0 0 0 9 0 0 0 4
  //   5195*0 8 7*0 2 0 0 4 80 4*0 40 6*0 2 0 0 4 20 6*0 10 10 6*0 80 40 8147*0 8 127*0 4 131*0 9 0 0 0 8
  //   123*0 21 0 0 0 8 123*0 81 0 0 0 8 123*0 6 0 0 0 8 123*0 24 0 0 0 8 123*0 84 0 0 0 8 123*0 12 0 0 0 8
  //   123*0 18 0 0 0 8 123*0 90 0 0 0 8 123*0 42 0 0 0 8 123*0 48 0 0 0 8 123*0 60 0 0 0 8 120*0 40 6*0 2
  //   0 0 4 2 0 0 0 8 112*0 40 6*0 2 0 0 4 8 0 0 0 8 112*0 40 6*0 2 0 0 4 20 0 0 0 8 112*0 40 6*0 2 0 0 4
  //   80 0 0 0 8 112*0 40 6*0 2 0 0 4 80 4*0 40 6*0 2 0 0 4 20 4*0 10 0 0 10 4*0 20 0 0 40 0 0 0 a 0 0 0 2
  //   76*0 40 6*0 2 0 0 4 80 4*0 40 6*0 2 0 0 4 20 4*0 10 0 0 10 4*0 20 0 0 40 0 0 0 a 0 0 0 8 332*0 40
  //   6*0 2 0 0 4 80 4*0 40 6*0 2 0 0 4 20 4*0 10 0 0 10 4*0 20 0 0 40 0 0 0 9 0 0 0 1 76*0 40 6*0 2 0 0 4
  //   80 4*0 40 6*0 2 0 0 4 20 4*0 10 0 0 10 4*0 20 0 0 40 0 0 0 9 0 0 0 4 5195*0 8 7*0 2 0 0 4 80 4*0 40
  //   6*0 2 0 0 4 20 6*0 10 10 6*0 80 40 8147*0 8 127*0 4 131*0 9 0 0 0 8 123*0 21 0 0 0 8 123*0 81 0 0 0
  //   8 123*0 6 0 0 0 8 123*0 24 0 0 0 8 123*0 84 0 0 0 8 123*0 12 0 0 0 8 123*0 18 0 0 0 8 123*0 90 0 0 0
  //   8 123*0 42 0 0 0 8 123*0 48 0 0 0 8 123*0 60 0 0 0 8 120*0 40 6*0 2 0 0 4 2 0 0 0 8 112*0 40 6*0 2 0
  //   0 4 8 0 0 0 8 112*0 40 6*0 2 0 0 4 20 0 0 0 8 112*0 40 6*0 2 0 0 4 80 0 0 0 8 112*0 40 6*0 2 0 0 4
  //   80 4*0 40 6*0 2 0 0 4 20 4*0 10 0 0 10 4*0 20 0 0 40 0 0 0 a 0 0 0 2 76*0 40 6*0 2 0 0 4 80 4*0 40
  //   6*0 2 0 0 4 20 4*0 10 0 0 10 4*0 20 0 0 40 0 0 0 a 0 0 0 8 332*0 40 6*0 2 0 0 4 80 4*0 40 6*0 2 0 0
  //   4 20 4*0 10 0 0 10 4*0 20 0 0 40 0 0 0 9 0 0 0 1 76*0 40 6*0 2 0 0 4 80 4*0 40 6*0 2 0 0 4 20 4*0 10
  //   0 0 10 4*0 20 0 0 40 0 0 0 9 0 0 0 4 5196*0 40 6*0 2 0 0 4 80 4*0 40 6*0 2 0 0 4 20 6*0 10 10 6*0 80
  //   40 8147*0 8 127*0 4 131*0 9 0 0 0 8 123*0 21 0 0 0 8 123*0 81 0 0 0 8 123*0 6 0 0 0 8 123*0 24 0 0 0
  //   8 123*0 84 0 0 0 8 123*0 12 0 0 0 8 123*0 18 0 0 0 8 123*0 90 0 0 0 8 123*0 42 0 0 0 8 123*0 48 0 0
  //   0 8 123*0 60 0 0 0 8 120*0 40 6*0 2 0 0 4 2 0 0 0 8 112*0 40 6*0 2 0 0 4 8 0 0 0 8 112*0 40 6*0 2 0
  //   0 4 20 0 0 0 8 112*0 40 6*0 2 0 0 4 80 0 0 0 8 112*0 40 6*0 2 0 0 4 80 4*0 40 6*0 2 0 0 4 20 4*0 10
  //   0 0 10 4*0 20 0 0 40 0 0 0 a 0 0 0 2 76*0 40 6*0 2 0 0 4 80 4*0 40 6*0 2 0 0 4 20 4*0 10 0 0 10 4*0
  //   20 0 0 40 0 0 0 a 0 0 0 8 332*0 40 6*0 2 0 0 4 80 4*0 40 6*0 2 0 0 4 20 4*0 10 0 0 10 4*0 20 0 0 40
  //   0 0 0 9 0 0 0 1 76*0 40 6*0 2 0 0 4 80 4*0 40 6*0 2 0 0 4 20 4*0 10 0 0 10 4*0 20 0 0 40 0 0 0 9 0 0
  //   0 4 5196*0 40 6*0 2 0 0 4 80 4*0 40 6*0 2 0 0 4 20 6*0 10 10 6*0 80 40 8147*0 8 127*0 4 131*0 9 0 0
  //   0 8 123*0 21 0 0 0 8 123*0 81 0 0 0 8 123*0 6 0 0 0 8 123*0 24 0 0 0 8 123*0 84 0 0 0 8 123*0 12 0 0
  //   0 8 123*0 18 0 0 0 8 123*0 90 0 0 0 8 123*0 42 0 0 0 8 123*0 48 0 0 0 8 123*0 60 0 0 0 8 120*0 40
  //   6*0 2 0 0 4 2 0 0 0 8 112*0 40 6*0 2 0 0 4 8 0 0 0 8 112*0 40 6*0 2 0 0 4 20 0 0 0 8 112*0 40 6*0 2
  //   0 0 4 80 0 0 0 8 112*0 40 6*0 2 0 0 4 80 4*0 40 6*0 2 0 0 4 20 4*0 10 0 0 10 4*0 20 0 0 40 0 0 0 a 0
  //   0 0 2 76*0 40 6*0 2 0 0 4 80 4*0 40 6*0 2 0 0 4 20 4*0 10 0 0 10 4*0 20 0 0 40 0 0 0 a 0 0 0 8 332*0
  //   40 6*0 2 0 0 4 80 4*0 40 6*0 2 0 0 4 20 4*0 10 0 0 10 4*0 20 0 0 40 0 0 0 9 0 0 0 1 76*0 40 6*0 2 0
  //   0 4 80 4*0 40 6*0 2 0 0 4 20 4*0 10 0 0 10 4*0 20 0 0 40 0 0 0 9 0 0 0 4 5195*0 8 7*0 2 0 0 4 80 4*0
  //   40 6*0 2 0 0 4 20 6*0 10 10 6*0 80 40 8147*0 8 127*0 4 131*0 9 0 0 0 8 123*0 21 0 0 0 8 123*0 81 0 0
  //   0 8 123*0 6 0 0 0 8 123*0 24 0 0 0 8 123*0 84 0 0 0 8 123*0 12 0 0 0 8 123*0 18 0 0 0 8 123*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
  //   NEXT_BIT
  //   ~CLR
  //   ~CLR
  //   ~OE
  //   SRCLK
  //   DATA
  //   RCLK
  //   NEXT_BIT
  //   DONE
  //   DATA BIT COUNTER
  //   CLR
  //   CE
  //   RESTART
endmodule

module Register (
  input  [7:0] DATA_BUS_IN,
  input  CLOCK,
  input  nDATA_LOAD,
  input  nDATA_OUT,
  output [7:0] CONTENTS_BUS_OUT,
  output [7:0] DATA_BUS_OUT
);

  // IC_74377 ic_74377_1: pin names not known; wires that end beside it: CLOCK, nDATA_LOAD, CONTENTS_BUS_OUT[0], CONTENTS_BUS_OUT[1], CONTENTS_BUS_OUT[2], CONTENTS_BUS_OUT[3], CONTENTS_BUS_OUT[4], CONTENTS_BUS_OUT[5], CONTENTS_BUS_OUT[6], CONTENTS_BUS_OUT[7]
  // IC_74244 ic_74244_1: pin names not known; wires that end beside it: CONTENTS_BUS_OUT[0], CONTENTS_BUS_OUT[1], CONTENTS_BUS_OUT[2], CONTENTS_BUS_OUT[3], CONTENTS_BUS_OUT[4], CONTENTS_BUS_OUT[5], CONTENTS_BUS_OUT[6], CONTENTS_BUS_OUT[7], nDATA_OUT, nDATA_OUT, DATA_BUS_OUT[0], DATA_BUS_OUT[1], DATA_BUS_OUT[2], DATA_BUS_OUT[3], DATA_BUS_OUT[4], DATA_BUS_OUT[5], DATA_BUS_OUT[6], DATA_BUS_OUT[7]
endmodule

module Program_Counter (
  input  PC_INC,
  input  PC_DEC,
  input  CLOCK,
  input  [7:0] PC_L_DATA_IN,
  input  nPC_L_OUT,
  input  nPC_L_LOAD,
  input  [7:0] PC_H_DATA_IN,
  input  nPC_H_OUT,
  input  nPC_H_LOAD,
  output [7:0] PC_L_DATA_OUT,
  output [15:0] MAR_BUS_OUT,
  output [7:0] PC_H_DATA_OUT
);

  wire DOWN_nUP, n74191_1_nrco, n74191_2_nrco, n74191_3_nrco, nCLK_EN, nor_2_out;

  nor nor_1 (DOWN_nUP, PC_INC, nor_2_out);
  nor nor_2 (nor_2_out, DOWN_nUP, PC_DEC);
  nor nor_3 (nCLK_EN, PC_INC, PC_DEC);
  _74191 u_74191_1 (
    .nU_D(DOWN_nUP), .CK(CLOCK), .nCTEN(nCLK_EN), .nPL(nPC_L_LOAD), .Q0(MAR_BUS_OUT[0]), .Q1(MAR_BUS_OUT[1]),
    .Q2(MAR_BUS_OUT[2]), .Q3(MAR_BUS_OUT[3]), .D0(PC_L_DATA_IN[0]), .D1(PC_L_DATA_IN[1]),
    .D2(PC_L_DATA_IN[2]), .D3(PC_L_DATA_IN[3]), .nRCO(n74191_1_nrco));  // open: TC
  _74191 u_74191_2 (
    .nU_D(DOWN_nUP), .CK(n74191_1_nrco), .nCTEN(nCLK_EN), .nPL(nPC_L_LOAD), .Q0(MAR_BUS_OUT[4]),
    .Q1(MAR_BUS_OUT[5]), .Q2(MAR_BUS_OUT[6]), .Q3(MAR_BUS_OUT[7]), .D0(PC_L_DATA_IN[4]),
    .D1(PC_L_DATA_IN[5]), .D2(PC_L_DATA_IN[6]), .D3(PC_L_DATA_IN[7]), .nRCO(n74191_2_nrco));  // open: TC
  _74191 u_74191_3 (
    .nU_D(DOWN_nUP), .CK(n74191_2_nrco), .nCTEN(nCLK_EN), .nPL(nPC_H_LOAD), .Q0(MAR_BUS_OUT[8]),
    .Q1(MAR_BUS_OUT[9]), .Q2(MAR_BUS_OUT[10]), .Q3(MAR_BUS_OUT[11]), .D0(PC_H_DATA_IN[0]),
    .D1(PC_H_DATA_IN[1]), .D2(PC_H_DATA_IN[2]), .D3(PC_H_DATA_IN[3]), .nRCO(n74191_3_nrco));  // open: TC
  _74191 u_74191_4 (
    .nU_D(DOWN_nUP), .CK(n74191_3_nrco), .nCTEN(nCLK_EN), .nPL(nPC_H_LOAD), .Q0(MAR_BUS_OUT[12]),
    .Q1(MAR_BUS_OUT[13]), .Q2(MAR_BUS_OUT[14]), .Q3(MAR_BUS_OUT[15]), .D0(PC_H_DATA_IN[4]),
    .D1(PC_H_DATA_IN[5]), .D2(PC_H_DATA_IN[6]), .D3(PC_H_DATA_IN[7]));  // open: TC, nRCO
  // IC_74244 ic_74244_1: pin names not known; wires that end beside it: MAR_BUS_OUT[0], MAR_BUS_OUT[1], MAR_BUS_OUT[2], MAR_BUS_OUT[3], MAR_BUS_OUT[4], MAR_BUS_OUT[5], MAR_BUS_OUT[6], MAR_BUS_OUT[7], nPC_L_OUT, nPC_L_OUT, PC_L_DATA_OUT[0], PC_L_DATA_OUT[1], PC_L_DATA_OUT[2], PC_L_DATA_OUT[3], PC_L_DATA_OUT[4], PC_L_DATA_OUT[5], PC_L_DATA_OUT[6], PC_L_DATA_OUT[7]
  // IC_74244 ic_74244_2: pin names not known; wires that end beside it: MAR_BUS_OUT[8], MAR_BUS_OUT[9], MAR_BUS_OUT[10], MAR_BUS_OUT[11], MAR_BUS_OUT[12], MAR_BUS_OUT[13], MAR_BUS_OUT[14], MAR_BUS_OUT[15], nPC_H_OUT, nPC_H_OUT, PC_H_DATA_OUT[0], PC_H_DATA_OUT[1], PC_H_DATA_OUT[2], PC_H_DATA_OUT[3], PC_H_DATA_OUT[4], PC_H_DATA_OUT[5], PC_H_DATA_OUT[6], PC_H_DATA_OUT[7]
endmodule

module Sequencer_Instruction_Decoder (
  input  [4:0] FLAGS_DATA_IN,
  input  [6:0] INSTRUCTION_DATA_IN,
  input  CLOCK,
  input  CLOCK_64X,
  input  LOAD,
  output nA_DATA_OUT,
  output nSTK_RESET,
  output nA_DATA_LOAD,
  output nALU_A_IN,
  output nB_DATA_OUT,
  output nALU_B_IN,
  output nB_DATA_LOAD,
  output ALU_S0,
  output nC_DATA_OUT,
  output ALU_S1,
  output nC_DATA_LOAD,
  output ALU_S2,
  output nD_DATA_OUT,
  output ALU_S3,
  output nD_DATA_LOAD,
  output ALU_M,
  output nFLAGS_LOAD,
  output ALU_Cn,
  output nIR_LOAD,
  output nALU_OUT,
  output nMAR_LB_LOAD,
  output PC_INC,
  output nMAR_HB_LOAD,
  output nMAR_PC_LOAD,
  output PC_DEC,
  output nMAR_STK_LOAD,
  output nPC_L_LOAD,
  output nMEM_RAM_LOAD,
  output nPC_H_LOAD,
  output nMEM_OUT,
  output nPC_L_OUT,
  output CLOCK_HALT,
  output nPC_H_OUT,
  output STK_INC,
  output STK_DEC
);

  wire A_DATA_LOAD, A_DATA_OUT, ALU_A_IN, ALU_B_IN, ALU_Cn_t, ALU_M_t, ALU_OUT, ALU_S0_t, ALU_S1_t, ALU_S2_t,
       ALU_S3_t, and_1_out, and_2_out, and_3_out, and_4_out, and_5_out, and_6_out, and_7_out, and_8_out,
       and_9_out, and_10_out, and_11_out, and_13_out, and_14_out, and_15_out, and_16_out, and_20_out,
       and_21_out, and_22_out, and_29_out, and_30_out, and_31_out, and_32_out, and_33_out, and_35_out,
       and_36_out, and_38_out, and_39_out, and_41_out, and_42_out, B_DATA_LOAD, B_DATA_OUT, C_DATA_LOAD,
       C_DATA_OUT, CLOCK_64X_out, CLOCK_HALT_t, D_DATA_LOAD, D_DATA_OUT, dip_7474_1_p1, dip_7474_1_p4,
       dip_7474_2_p2, dip_74161_1_p1, dip_74161_2_p1, dip_74161_2_p3, dip_74161_2_p5, dip_74161_2_p7,
       dip_74161_2_p9, dip_74161_2_p13, dip_74161_3_p2, dip_74161_3_p9, dip_74161_3_p13, dip_74595_1_p2,
       dip_74595_1_p6, dip_74595_1_p10, dip_74595_2_p6, dip_74595_3_p6, dip_74595_4_p6, dip_74595_5_p6, DONE,
       FLAGS_LOAD, IN_OUT, IR_LOAD, LOAD_t, MAR_HB_LOAD, MAR_LB_LOAD, MAR_PC_LOAD, MAR_STK_LOAD, MEM_OUT,
       MEM_RAM_LOAD, n74165_1_p1, n74165_1_p2, n74165_1_p13, nor_3_out, not_25_out, not_28_out, not_29_out,
       not_30_out, not_31_out, not_34_out, not_35_out, not_36_out, or_1_out, or_4_out, or_5_out, or_6_out,
       or_7_out, OUT1_IN, OUT2_IN, PC_DEC_t, PC_H_LOAD, PC_H_OUT, PC_INC_t, PC_L_LOAD, PC_L_OUT, STK_DEC_t,
       STK_INC_t, STK_RESET, TSTATE_0, TSTATE_1, TSTATE_RESET, TSTATE_RESET_CLOCKED;
  wire [2:0] BANK;
  wire [3:0] T_STATE, undriven, undriven_2;
  wire [3:3] undriven_3;
  wire [7:0] dip_74595_1_p12, dip_74595_2_p8, dip_74595_3_p8, dip_74595_4_p8, dip_74595_5_p8, dip_74595_6_p9,
       rom_1_data;

  // Probe on FLAGS_DATA_IN[4]
  // Probe on FLAGS_DATA_IN[3]
  Clock_Divider clock_divider_1 (.CLOCK(CLOCK_64X_out));  // open: CLOCK_DIV8, CLOCK_DIV64
  Clock u_CLOCK_64X (.out(CLOCK_64X_out));
  not not_1 (nA_DATA_OUT, and_1_out);
  not not_2 (nA_DATA_LOAD, and_2_out);
  not not_3 (nB_DATA_OUT, and_3_out);
  not not_4 (nB_DATA_LOAD, and_4_out);
  not not_5 (nC_DATA_OUT, and_5_out);
  not not_6 (nC_DATA_LOAD, and_6_out);
  not not_7 (nD_DATA_OUT, and_7_out);
  not not_8 (nD_DATA_LOAD, and_8_out);
  not not_9 (nFLAGS_LOAD, and_9_out);
  not not_10 (nIR_LOAD, or_1_out);
  not not_11 (nPC_L_LOAD, and_13_out);
  not not_12 (nPC_H_LOAD, and_14_out);
  not not_13 (nPC_L_OUT, and_15_out);
  not not_14 (nPC_H_OUT, and_16_out);
  // Probe on FLAGS_DATA_IN[1]
  // Probe on FLAGS_DATA_IN[2]
  and and_1 (and_1_out, A_DATA_OUT, 1'b1);
  and and_2 (and_2_out, A_DATA_LOAD, 1'b1);
  and and_3 (and_3_out, B_DATA_OUT, 1'b1);
  and and_4 (and_4_out, B_DATA_LOAD, 1'b1);
  and and_5 (and_5_out, C_DATA_OUT, 1'b1);
  and and_6 (and_6_out, C_DATA_LOAD, 1'b1);
  and and_7 (and_7_out, D_DATA_OUT, 1'b1);
  and and_8 (and_8_out, D_DATA_LOAD, 1'b1);
  and and_9 (and_9_out, FLAGS_LOAD, 1'b1);
  and and_10 (and_10_out, IR_LOAD, 1'b1);
  or or_1 (or_1_out, and_10_out, TSTATE_1);
  and and_11 (and_11_out, PC_INC_t, 1'b1);
  or or_2 (PC_INC, and_11_out, TSTATE_1);
  and and_12 (PC_DEC, PC_DEC_t, 1'b1);
  and and_13 (and_13_out, PC_L_LOAD, 1'b1);
  and and_14 (and_14_out, PC_H_LOAD, 1'b1);
  and and_15 (and_15_out, PC_L_OUT, 1'b1);
  and and_16 (and_16_out, PC_H_OUT, 1'b1);
  and and_17 (STK_INC, STK_INC_t, 1'b1);
  and and_18 (STK_DEC, STK_DEC_t, 1'b1);
  and and_19 (TSTATE_RESET_CLOCKED, TSTATE_RESET, 1'b1);
  // Probe on INSTRUCTION_DATA_IN[5]
  // Probe on INSTRUCTION_DATA_IN[6]
  // Probe on FLAGS_DATA_IN[0]
  // Probe on INSTRUCTION_DATA_IN[2]
  // Probe on INSTRUCTION_DATA_IN[3]
  // Probe on INSTRUCTION_DATA_IN[4]
  // Probe on INSTRUCTION_DATA_IN[0]
  // Probe on INSTRUCTION_DATA_IN[1]
  // DIP_7474 dip_7474_1: pin names not known; wires that end beside it: dip_7474_1_p1, DONE, DONE, dip_7474_1_p4, dip_7474_1_p4
  or or_3 (dip_7474_1_p1, not_25_out, DONE);
  // Probe on T_STATE[1]
  // Probe on T_STATE[2]
  // Probe on T_STATE[3]
  not not_15 (nSTK_RESET, and_20_out);
  and and_20 (and_20_out, STK_RESET, 1'b1);
  and and_21 (and_21_out, ALU_A_IN, 1'b1);
  not not_16 (nALU_A_IN, and_21_out);
  not not_17 (nALU_B_IN, and_22_out);
  and and_22 (and_22_out, ALU_B_IN, 1'b1);
  and and_23 (ALU_S0, ALU_S0_t, 1'b1);
  and and_24 (ALU_S1, ALU_S1_t, 1'b1);
  and and_25 (ALU_S2, ALU_S2_t, 1'b1);
  and and_26 (ALU_S3, ALU_S3_t, 1'b1);
  and and_27 (ALU_M, ALU_M_t, 1'b1);
  and and_28 (ALU_Cn, ALU_Cn_t, 1'b1);
  and and_29 (and_29_out, ALU_OUT, 1'b1);
  not not_18 (nALU_OUT, and_29_out);
  and and_30 (and_30_out, MAR_LB_LOAD, 1'b1);
  not not_19 (nMAR_LB_LOAD, and_30_out);
  not not_20 (nMAR_HB_LOAD, and_31_out);
  and and_31 (and_31_out, MAR_HB_LOAD, 1'b1);
  not not_21 (nMAR_PC_LOAD, or_4_out);
  and and_32 (and_32_out, MAR_STK_LOAD, 1'b1);
  not not_22 (nMAR_STK_LOAD, and_32_out);
  and and_33 (and_33_out, MEM_RAM_LOAD, 1'b1);
  not not_23 (nMEM_RAM_LOAD, and_33_out);
  not not_24 (nMEM_OUT, or_5_out);
  and and_34 (CLOCK_HALT, CLOCK_HALT_t, 1'b1);
  not not_25 (not_25_out, LOAD_t);
  // Probe on T_STATE[0]
  and and_35 (and_35_out, MAR_PC_LOAD, 1'b1);
  or or_4 (or_4_out, and_35_out, TSTATE_0);
  and and_36 (and_36_out, MEM_OUT, 1'b1);
  or or_5 (or_5_out, and_36_out, TSTATE_1);
  // DIP_74161 dip_74161_1: pin names not known; wires that end beside it: dip_74161_1_p1, CLOCK, T_STATE[0], 1'b0, T_STATE[1], 1'b0, T_STATE[3], 1'b0, T_STATE[2], 1'b0, 1'b1, 1'b1, 1'b1
  not not_26 (dip_74161_1_p1, TSTATE_RESET_CLOCKED);
  DotMatrix #(.matrixcols(4), .matrixrows(1), .dotshape("circle")) dotmatrix_1 (
    .col0(T_STATE[2]), .col1(T_STATE[3]), .col2(T_STATE[1]), .col3(T_STATE[0]));
  ROM #(.addrWidth(19)) rom_1 (
    .addr({FLAGS_DATA_IN, INSTRUCTION_DATA_IN, T_STATE, BANK}), .data(rom_1_data), .sel(1'b1));
  // _74165 74165_1: pin names not known; wires that end beside it: n74165_1_p1, n74165_1_p2, rom_1_data[4], rom_1_data[5], rom_1_data[6], rom_1_data[7], 1'b0, rom_1_data[3], rom_1_data[2], rom_1_data[1], rom_1_data[0], 1'b0, n74165_1_p13
  nor nor_1 (n74165_1_p1, LOAD_t, and_39_out);
  not not_27 (LOAD_t, CLOCK);
  and and_37 (TSTATE_1, T_STATE[0], nor_3_out);
  nor nor_2 (TSTATE_0, T_STATE[0], T_STATE[1], T_STATE[2], T_STATE[3]);
  nor nor_3 (nor_3_out, T_STATE[1], T_STATE[2], T_STATE[3]);
  and and_38 (and_38_out, DONE, not_28_out);
  not not_28 (not_28_out, CLOCK_64X);
  // IC_74377 ic_74377_1: pin names not known
  not not_29 (not_29_out, and_38_out);
  Hex_Digit_Display hex_digit_display_1 (.value(undriven));  // open: dp
  Hex_Digit_Display hex_digit_display_2 (.value(undriven_2));  // open: dp
  // IC_74377 ic_74377_2: pin names not known; wires that end beside it: and_38_out, not_29_out
  // DIP_74595 dip_74595_1: pin names not known; wires that end beside it: dip_74595_1_p12[7], dip_74595_1_p2, dip_74595_1_p12[6], n74165_1_p2, dip_74595_1_p12[5], dip_74595_1_p6, dip_74595_1_p12[4], 1'b0, dip_74595_1_p12[3], dip_74595_1_p10, dip_74595_1_p12[2], dip_74595_1_p12[0], dip_74595_1_p12[1], dip_74595_1_p10, dip_74595_2_p8[7], dip_74595_1_p2, dip_74595_2_p8[6], n74165_1_p2
  Hex_Digit_Display hex_digit_display_3 (.value({TSTATE_RESET, CLOCK_HALT_t, MEM_OUT, MEM_RAM_LOAD}));  // open: dp
  Hex_Digit_Display hex_digit_display_4 (.value({undriven_3[3], OUT2_IN, OUT1_IN, IN_OUT}));  // open: dp
  // IC_74377 ic_74377_3: pin names not known
  // DIP_74595 dip_74595_2: pin names not known; wires that end beside it: dip_74595_2_p8[5], dip_74595_1_p6, dip_74595_2_p8[4], 1'b0, dip_74595_2_p8[3], dip_74595_2_p6, dip_74595_2_p8[2], dip_74595_2_p8[0], dip_74595_2_p8[1], dip_74595_2_p6, dip_74595_3_p8[7], dip_74595_1_p2, dip_74595_3_p8[6], n74165_1_p2
  Hex_Digit_Display hex_digit_display_5 (.value({ALU_OUT, ALU_Cn_t, ALU_M_t, ALU_S3_t}));  // open: dp
  Hex_Digit_Display hex_digit_display_6 (.value({MAR_STK_LOAD, MAR_PC_LOAD, MAR_HB_LOAD, MAR_LB_LOAD}));  // open: dp
  // IC_74377 ic_74377_4: pin names not known; wires that end beside it: and_38_out, not_29_out, and_38_out, not_29_out
  // DIP_74595 dip_74595_3: pin names not known; wires that end beside it: dip_74595_3_p8[5], dip_74595_1_p6, dip_74595_3_p8[4], 1'b0, dip_74595_3_p8[3], dip_74595_3_p6, dip_74595_3_p8[2], dip_74595_3_p8[0], dip_74595_3_p8[1], dip_74595_3_p6, dip_74595_4_p8[7], dip_74595_1_p2, dip_74595_4_p8[6], n74165_1_p2
  and and_39 (and_39_out, and_42_out, CLOCK_64X);
  Hex_Digit_Display hex_digit_display_7 (.value({ALU_A_IN, STK_RESET, STK_DEC_t, STK_INC_t}));  // open: dp
  Hex_Digit_Display hex_digit_display_8 (.value({ALU_S2_t, ALU_S1_t, ALU_S0_t, ALU_B_IN}));  // open: dp
  // IC_74377 ic_74377_5: pin names not known
  // DIP_74595 dip_74595_4: pin names not known; wires that end beside it: dip_74595_4_p8[5], dip_74595_1_p6, dip_74595_4_p8[4], 1'b0, dip_74595_4_p8[3], dip_74595_4_p6, dip_74595_4_p8[2], dip_74595_4_p8[0], dip_74595_4_p8[1], dip_74595_4_p6, dip_74595_5_p8[7], dip_74595_1_p2, dip_74595_5_p8[6], n74165_1_p2
  nor nor_4 (dip_74595_1_p2, n74165_1_p1, or_6_out);
  or or_6 (or_6_out, and_42_out, not_30_out);
  not not_30 (not_30_out, CLOCK_64X);
  Hex_Digit_Display hex_digit_display_9 (.value({PC_H_OUT, PC_L_OUT, PC_H_LOAD, PC_L_LOAD}));  // open: dp
  Hex_Digit_Display hex_digit_display_10 (.value({PC_DEC_t, PC_INC_t, IR_LOAD, FLAGS_LOAD}));  // open: dp
  // IC_74377 ic_74377_6: pin names not known; wires that end beside it: and_38_out, not_29_out, and_38_out, not_29_out, and_38_out
  // DIP_74595 dip_74595_5: pin names not known; wires that end beside it: dip_74595_5_p8[5], dip_74595_1_p6, dip_74595_5_p8[4], 1'b0, dip_74595_5_p8[3], dip_74595_5_p6, dip_74595_5_p8[2], dip_74595_5_p8[0], dip_74595_5_p8[1], dip_74595_5_p6, dip_74595_6_p9[7], dip_74595_1_p2, dip_74595_6_p9[6], n74165_1_p2
  and and_40 (n74165_1_p2, and_41_out, not_31_out);
  and and_41 (and_41_out, or_7_out, CLOCK_64X);
  not not_31 (not_31_out, DONE);
  or or_7 (or_7_out, n74165_1_p1, and_42_out);
  Hex_Digit_Display hex_digit_display_11 (.value({B_DATA_LOAD, B_DATA_OUT, A_DATA_LOAD, A_DATA_OUT}));  // open: dp
  Hex_Digit_Display hex_digit_display_12 (.value({D_DATA_LOAD, D_DATA_OUT, C_DATA_LOAD, C_DATA_OUT}));  // open: dp
  // DIP_74595 dip_74595_6: pin names not known; wires that end beside it: dip_74595_6_p9[5], dip_74595_1_p6, not_29_out, dip_74595_6_p9[4], 1'b0, dip_74595_6_p9[3], n74165_1_p13, dip_74595_6_p9[2], dip_74595_6_p9[0], dip_74595_6_p9[1]
  not not_32 (dip_74595_1_p6, n74165_1_p2);
  and and_42 (and_42_out, dip_74161_2_p3, dip_74161_2_p5, dip_74161_2_p7);
  DotMatrix #(.matrixcols(4), .matrixrows(1), .dotshape("circle")) dotmatrix_2 (
    .col0(dip_74161_2_p9), .col1(dip_74161_2_p7), .col2(dip_74161_2_p5), .col3(dip_74161_2_p3));
  // DIP_74161 dip_74161_2: pin names not known; wires that end beside it: dip_74161_2_p1, n74165_1_p2, dip_74161_2_p3, 1'b0, dip_74161_2_p5, 1'b0, dip_74161_2_p7, 1'b0, dip_74161_2_p9, 1'b0, 1'b1, 1'b1, dip_74161_2_p13
  or or_8 (dip_74161_2_p1, and_42_out, n74165_1_p1);
  not not_33 (dip_74161_2_p13, and_42_out);
  not not_34 (not_34_out, dip_74595_1_p2);
  // AND_Gate and_43 has open pins: in1=n74165_1_p2, out=open
  not not_35 (not_35_out, and_42_out);
  not not_36 (not_36_out, CLOCK_64X);
  DotMatrix #(.matrixcols(4), .matrixrows(1), .dotshape("circle")) dotmatrix_3 (
    .col0(dip_74161_3_p9), .col1(BANK[2]), .col2(BANK[1]), .col3(BANK[0]));
  // DIP_74161 dip_74161_3: pin names not known; wires that end beside it: not_34_out, dip_74161_3_p2, BANK[0], 1'b0, BANK[1], 1'b0, BANK[2], 1'b0, dip_74161_3_p9, 1'b0, 1'b1, 1'b1, dip_74161_3_p13
  nor nor_5 (dip_74161_3_p2, not_35_out, n74165_1_p2, not_36_out);
  // NOT_Gate not_37 is placed but not wired
  // DIP_7474 dip_7474_2: pin names not known; wires that end beside it: CLOCK, dip_7474_2_p2, dip_7474_2_p2, DONE
  not not_38 (dip_74161_3_p13, 1'b0);
  and and_44 (dip_7474_2_p2, BANK[1], BANK[2]);

  // Other names for the same wires on the sheet: FLAGS[4:0] = FLAGS_DATA_IN; INSTRUCTION[6:0] = INSTRUCTION_DATA_IN

  // Notes on the sheet:
  //   LOAD: pull=down
  //   T-STATE COUNTER
  //   CONTROL ROM
  //   ROM DATA
  //   contents of rom_1 (hex, n*v repeats v):
  //   17*0 8 127*0 4 131*0 9 0 0 0 8 123*0 21 0 0 0 8 123*0 81 0 0 0 8 123*0 6 0 0 0 8 123*0 24 0 0 0 8
  //   123*0 84 0 0 0 8 123*0 12 0 0 0 8 123*0 18 0 0 0 8 123*0 90 0 0 0 8 123*0 42 0 0 0 8 123*0 48 0 0 0
  //   8 123*0 60 0 0 0 8 120*0 40 6*0 2 0 0 4 2 0 0 0 8 112*0 40 6*0 2 0 0 4 8 0 0 0 8 112*0 40 6*0 2 0 0
  //   4 20 0 0 0 8 112*0 40 6*0 2 0 0 4 80 0 0 0 8 112*0 40 6*0 2 0 0 4 80 4*0 40 6*0 2 0 0 4 20 4*0 10 0
  //   0 10 4*0 20 0 0 40 0 0 0 a 0 0 0 2 76*0 40 6*0 2 0 0 4 80 4*0 40 6*0 2 0 0 4 20 4*0 10 0 0 10 4*0 20
  //   0 0 40 0 0 0 a 0 0 0 8 332*0 40 6*0 2 0 0 4 80 4*0 40 6*0 2 0 0 4 20 4*0 10 0 0 10 4*0 20 0 0 40 0 0
  //   0 9 0 0 0 1 76*0 40 6*0 2 0 0 4 80 4*0 40 6*0 2 0 0 4 20 4*0 10 0 0 10 4*0 20 0 0 40 0 0 0 9 0 0 0 4
  //   5195*0 8 7*0 2 0 0 4 80 4*0 40 6*0 2 0 0 4 20 6*0 10 10 6*0 80 40 8147*0 8 127*0 4 131*0 9 0 0 0 8
  //   123*0 21 0 0 0 8 123*0 81 0 0 0 8 123*0 6 0 0 0 8 123*0 24 0 0 0 8 123*0 84 0 0 0 8 123*0 12 0 0 0 8
  //   123*0 18 0 0 0 8 123*0 90 0 0 0 8 123*0 42 0 0 0 8 123*0 48 0 0 0 8 123*0 60 0 0 0 8 120*0 40 6*0 2
  //   0 0 4 2 0 0 0 8 112*0 40 6*0 2 0 0 4 8 0 0 0 8 112*0 40 6*0 2 0 0 4 20 0 0 0 8 112*0 40 6*0 2 0 0 4
  //   80 0 0 0 8 112*0 40 6*0 2 0 0 4 80 4*0 40 6*0 2 0 0 4 20 4*0 10 0 0 10 4*0 20 0 0 40 0 0 0 a 0 0 0 2
  //   76*0 40 6*0 2 0 0 4 80 4*0 40 6*0 2 0 0 4 20 4*0 10 0 0 10 4*0 20 0 0 40 0 0 0 a 0 0 0 8 332*0 40
  //   6*0 2 0 0 4 80 4*0 40 6*0 2 0 0 4 20 4*0 10 0 0 10 4*0 20 0 0 40 0 0 0 9 0 0 0 1 76*0 40 6*0 2 0 0 4
  //   80 4*0 40 6*0 2 0 0 4 20 4*0 10 0 0 10 4*0 20 0 0 40 0 0 0 9 0 0 0 4 5195*0 8 7*0 2 0 0 4 80 4*0 40
  //   6*0 2 0 0 4 20 6*0 10 10 6*0 80 40 8147*0 8 127*0 4 131*0 9 0 0 0 8 123*0 21 0 0 0 8 123*0 81 0 0 0
  //   8 123*0 6 0 0 0 8 123*0 24 0 0 0 8 123*0 84 0 0 0 8 123*0 12 0 0 0 8 123*0 18 0 0 0 8 123*0 90 0 0 0
  //   8 123*0 42 0 0 0 8 123*0 48 0 0 0 8 123*0 60 0 0 0 8 120*0 40 6*0 2 0 0 4 2 0 0 0 8 112*0 40 6*0 2 0
  //   0 4 8 0 0 0 8 112*0 40 6*0 2 0 0 4 20 0 0 0 8 112*0 40 6*0 2 0 0 4 80 0 0 0 8 112*0 40 6*0 2 0 0 4
  //   80 4*0 40 6*0 2 0 0 4 20 4*0 10 0 0 10 4*0 20 0 0 40 0 0 0 a 0 0 0 2 76*0 40 6*0 2 0 0 4 80 4*0 40
  //   6*0 2 0 0 4 20 4*0 10 0 0 10 4*0 20 0 0 40 0 0 0 a 0 0 0 8 332*0 40 6*0 2 0 0 4 80 4*0 40 6*0 2 0 0
  //   4 20 4*0 10 0 0 10 4*0 20 0 0 40 0 0 0 9 0 0 0 1 76*0 40 6*0 2 0 0 4 80 4*0 40 6*0 2 0 0 4 20 4*0 10
  //   0 0 10 4*0 20 0 0 40 0 0 0 9 0 0 0 4 5196*0 40 6*0 2 0 0 4 80 4*0 40 6*0 2 0 0 4 20 6*0 10 10 6*0 80
  //   40 8147*0 8 127*0 4 131*0 9 0 0 0 8 123*0 21 0 0 0 8 123*0 81 0 0 0 8 123*0 6 0 0 0 8 123*0 24 0 0 0
  //   8 123*0 84 0 0 0 8 123*0 12 0 0 0 8 123*0 18 0 0 0 8 123*0 90 0 0 0 8 123*0 42 0 0 0 8 123*0 48 0 0
  //   0 8 123*0 60 0 0 0 8 120*0 40 6*0 2 0 0 4 2 0 0 0 8 112*0 40 6*0 2 0 0 4 8 0 0 0 8 112*0 40 6*0 2 0
  //   0 4 20 0 0 0 8 112*0 40 6*0 2 0 0 4 80 0 0 0 8 112*0 40 6*0 2 0 0 4 80 4*0 40 6*0 2 0 0 4 20 4*0 10
  //   0 0 10 4*0 20 0 0 40 0 0 0 a 0 0 0 2 76*0 40 6*0 2 0 0 4 80 4*0 40 6*0 2 0 0 4 20 4*0 10 0 0 10 4*0
  //   20 0 0 40 0 0 0 a 0 0 0 8 332*0 40 6*0 2 0 0 4 80 4*0 40 6*0 2 0 0 4 20 4*0 10 0 0 10 4*0 20 0 0 40
  //   0 0 0 9 0 0 0 1 76*0 40 6*0 2 0 0 4 80 4*0 40 6*0 2 0 0 4 20 4*0 10 0 0 10 4*0 20 0 0 40 0 0 0 9 0 0
  //   0 4 5196*0 40 6*0 2 0 0 4 80 4*0 40 6*0 2 0 0 4 20 6*0 10 10 6*0 80 40 8147*0 8 127*0 4 131*0 9 0 0
  //   0 8 123*0 21 0 0 0 8 123*0 81 0 0 0 8 123*0 6 0 0 0 8 123*0 24 0 0 0 8 123*0 84 0 0 0 8 123*0 12 0 0
  //   0 8 123*0 18 0 0 0 8 123*0 90 0 0 0 8 123*0 42 0 0 0 8 123*0 48 0 0 0 8 123*0 60 0 0 0 8 120*0 40
  //   6*0 2 0 0 4 2 0 0 0 8 112*0 40 6*0 2 0 0 4 8 0 0 0 8 112*0 40 6*0 2 0 0 4 20 0 0 0 8 112*0 40 6*0 2
  //   0 0 4 80 0 0 0 8 112*0 40 6*0 2 0 0 4 80 4*0 40 6*0 2 0 0 4 20 4*0 10 0 0 10 4*0 20 0 0 40 0 0 0 a 0
  //   0 0 2 76*0 40 6*0 2 0 0 4 80 4*0 40 6*0 2 0 0 4 20 4*0 10 0 0 10 4*0 20 0 0 40 0 0 0 a 0 0 0 8 332*0
  //   40 6*0 2 0 0 4 80 4*0 40 6*0 2 0 0 4 20 4*0 10 0 0 10 4*0 20 0 0 40 0 0 0 9 0 0 0 1 76*0 40 6*0 2 0
  //   0 4 80 4*0 40 6*0 2 0 0 4 20 4*0 10 0 0 10 4*0 20 0 0 40 0 0 0 9 0 0 0 4 5195*0 8 7*0 2 0 0 4 80 4*0
  //   40 6*0 2 0 0 4 20 6*0 10 10 6*0 80 40 8147*0 8 127*0 4 131*0 9 0 0 0 8 123*0 21 0 0 0 8 123*0 81 0 0
  //   0 8 123*0 6 0 0 0 8 123*0 24 0 0 0 8 123*0 84 0 0 0 8 123*0 12 0 0 0 8 123*0 18 0 0 0 8 123*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
  //   SH/~LR
  //   DATA
  //   NEXT_BIT
  //   ~CLR
  //   ~CLR
  //   ~OE
  //   SRCLK
  //   DATA
  //   RCLK
  //   NEXT_BIT
  //   DONE
  //   DATA BIT COUNTER
  //   CLR
  //   CE
  //   CLR
  //   RESTART
  //   DATA BYTE COUNTER
  //   CE
  //   RESTART
endmodule

module Stack_Pointer (
  input  STK_INC,
  input  STK_DEC,
  input  CLOCK,
  input  nSTK_RESET,
  output [15:0] MAR_BUS_OUT
);

  wire DOWN_nUP, n74191_1_nrco, nCLK_EN, nor_2_out;

  nor nor_1 (DOWN_nUP, STK_INC, nor_2_out);
  nor nor_2 (nor_2_out, DOWN_nUP, STK_DEC);
  nor nor_3 (nCLK_EN, STK_INC, STK_DEC);
  _74191 u_74191_1 (
    .nU_D(DOWN_nUP), .CK(CLOCK), .nCTEN(nCLK_EN), .nPL(nSTK_RESET), .Q0(MAR_BUS_OUT[0]), .Q1(MAR_BUS_OUT[1]),
    .Q2(MAR_BUS_OUT[2]), .Q3(MAR_BUS_OUT[3]), .D0(1'b0), .D1(1'b0), .D2(1'b0), .D3(1'b0), .nRCO(n74191_1_nrco));  // open: TC
  _74191 u_74191_2 (
    .nU_D(DOWN_nUP), .CK(n74191_1_nrco), .nCTEN(nCLK_EN), .nPL(nSTK_RESET), .Q0(MAR_BUS_OUT[4]),
    .Q1(MAR_BUS_OUT[5]), .Q2(MAR_BUS_OUT[6]), .Q3(MAR_BUS_OUT[7]), .D0(1'b0), .D1(1'b0), .D2(1'b0), .D3(1'b0));  // open: TC, nRCO

  assign MAR_BUS_OUT[15:8] = {8{1'b1}};
endmodule

module ALU (
  input  [7:0] DATA_BUS_IN,
  input  CLOCK,
  input  nA_IN,
  input  nB_IN,
  input  S3,
  input  S2,
  input  S1,
  input  S0,
  input  M,
  input  Cn,
  input  nALU_OUT,
  output Flt,
  output Feq,
  output Fgt,
  output [7:0] DATA_BUS_OUT,
  output Fz,
  output [7:0] CONTENTS_BUS_OUT,
  output Fc
);

  wire ALU_OUT, and_1_out, and_2_out, and_4_out, ic_74377_1_p1, ic_74377_1_p2, ic_74377_1_p3, ic_74377_1_p4,
       ic_74377_1_p5, ic_74377_1_p6, ic_74377_1_p7, ic_74377_1_p8, ic_74377_2_p5, ic_74377_2_p6,
       ic_74377_2_p7, ic_74377_2_p8, ic_74377_2_p9, ic_74377_2_p10, ic_74377_2_p11, ic_74377_2_p12,
       n74181_1_p18, n74181_1_p19, n74181_2_p18, n74181_2_p19, nor_1_out, not_1_out, not_2_out, not_3_out,
       or_1_out, or_2_out;

  // IC_74377 ic_74377_1: pin names not known; wires that end beside it: ic_74377_1_p1, ic_74377_1_p2, ic_74377_1_p3, ic_74377_1_p4, ic_74377_1_p5, ic_74377_1_p6, ic_74377_1_p7, ic_74377_1_p8
  // IC_74377 ic_74377_2: pin names not known; wires that end beside it: CLOCK, nA_IN, CLOCK, nB_IN, ic_74377_2_p5, ic_74377_2_p6, ic_74377_2_p7, ic_74377_2_p8, ic_74377_2_p9, ic_74377_2_p10, ic_74377_2_p11, ic_74377_2_p12
  // _74181 74181_1: pin names not known; wires that end beside it: ic_74377_2_p5, ic_74377_1_p1, S3, S2, S1, S0, Cn, M, CONTENTS_BUS_OUT[0], CONTENTS_BUS_OUT[1], CONTENTS_BUS_OUT[2], ic_74377_1_p2, ic_74377_2_p6, ic_74377_1_p3, ic_74377_2_p7, ic_74377_1_p4, ic_74377_2_p8, n74181_1_p18, n74181_1_p19, CONTENTS_BUS_OUT[3]
  // _74181 74181_2: pin names not known; wires that end beside it: ic_74377_2_p9, ic_74377_1_p5, S3, S2, S1, S0, n74181_1_p18, M, CONTENTS_BUS_OUT[4], CONTENTS_BUS_OUT[5], CONTENTS_BUS_OUT[6], ic_74377_1_p6, ic_74377_2_p10, ic_74377_1_p7, ic_74377_2_p11, ic_74377_1_p8, ic_74377_2_p12, n74181_2_p18, n74181_2_p19, CONTENTS_BUS_OUT[7]
  not not_1 (not_1_out, n74181_2_p18);
  and and_1 (and_1_out, n74181_1_p18, n74181_2_p18);
  or or_1 (or_1_out, and_1_out, n74181_2_p18);
  and and_2 (and_2_out, n74181_1_p19, n74181_2_p19);
  not not_2 (not_2_out, n74181_1_p18);
  not not_3 (not_3_out, n74181_2_p18);
  and and_3 (Fc, not_1_out, ALU_OUT);
  and and_4 (and_4_out, not_2_out, not_3_out);
  and and_5 (Flt, ALU_OUT, or_1_out);
  and and_6 (Feq, ALU_OUT, and_2_out);
  or or_2 (or_2_out, and_4_out, not_3_out);
  and and_7 (Fgt, ALU_OUT, or_2_out);
  nor nor_1 (nor_1_out, CONTENTS_BUS_OUT[0], CONTENTS_BUS_OUT[1], CONTENTS_BUS_OUT[2], CONTENTS_BUS_OUT[3], CONTENTS_BUS_OUT[4], CONTENTS_BUS_OUT[5], CONTENTS_BUS_OUT[6], CONTENTS_BUS_OUT[7]);
  and and_8 (Fz, ALU_OUT, nor_1_out);
  // IC_74244 ic_74244_1: pin names not known; wires that end beside it: CONTENTS_BUS_OUT[0], CONTENTS_BUS_OUT[1], CONTENTS_BUS_OUT[2], CONTENTS_BUS_OUT[3], CONTENTS_BUS_OUT[4], CONTENTS_BUS_OUT[5], CONTENTS_BUS_OUT[6], CONTENTS_BUS_OUT[7], nALU_OUT, nALU_OUT, DATA_BUS_OUT[0], DATA_BUS_OUT[1], DATA_BUS_OUT[2], DATA_BUS_OUT[3], DATA_BUS_OUT[4], DATA_BUS_OUT[5], DATA_BUS_OUT[6], DATA_BUS_OUT[7]
  not not_4 (ALU_OUT, nALU_OUT);

  // Notes on the sheet:
  //   M=0   Cn=0   S=0110  (A < B)
  //   M=0   Cn=1   S=0110  (A=B)
  //   M=0   Cn=1   S=0110  (A>B)
endmodule

module Memory_Access_Register (
  input  [7:0] LB_DATA_IN,
  input  CLOCK,
  input  nLB_LOAD,
  input  [7:0] HB_DATA_IN,
  input  nHB_LOAD,
  input  [15:0] PC_DATA_IN,
  input  [15:0] STK_DATA_IN,
  input  nPC_LOAD,
  input  nSTK_LOAD,
  output [15:0] DATA_OUT
);

  wire and_1_out, and_3_out, High_byte_p13, High_byte_p14, High_byte_p15, High_byte_p16, High_byte_p17,
       High_byte_p18, High_byte_p19, High_byte_p20, Low_byte_p9, Low_byte_p10, Low_byte_p11, Low_byte_p12,
       Low_byte_p13, Low_byte_p14, Low_byte_p15, Low_byte_p16, nHIGH_LOAD, nLOW_LOAD;

  // IC_74244 Low_byte: pin names not known; wires that end beside it: LB_DATA_IN[0], LB_DATA_IN[1], LB_DATA_IN[2], LB_DATA_IN[3], LB_DATA_IN[4], LB_DATA_IN[5], LB_DATA_IN[6], LB_DATA_IN[7], Low_byte_p9, Low_byte_p10, Low_byte_p11, Low_byte_p12, Low_byte_p13, Low_byte_p14, Low_byte_p15, Low_byte_p16
  // IC_74244 High_byte: pin names not known; wires that end beside it: nLB_LOAD, nLB_LOAD, HB_DATA_IN[0], HB_DATA_IN[1], HB_DATA_IN[2], HB_DATA_IN[3], HB_DATA_IN[4], HB_DATA_IN[5], HB_DATA_IN[6], HB_DATA_IN[7], nHB_LOAD, nHB_LOAD, High_byte_p13, High_byte_p14, High_byte_p15, High_byte_p16, High_byte_p17, High_byte_p18, High_byte_p19, High_byte_p20
  // IC_74244 Low_byte_2: pin names not known; wires that end beside it: PC_DATA_IN[0], PC_DATA_IN[1], PC_DATA_IN[2], PC_DATA_IN[3], PC_DATA_IN[4], PC_DATA_IN[5], PC_DATA_IN[6], PC_DATA_IN[7], Low_byte_p9, Low_byte_p10, Low_byte_p11, Low_byte_p12, Low_byte_p13, Low_byte_p14, Low_byte_p15, Low_byte_p16
  // IC_74244 High_byte_2: pin names not known; wires that end beside it: nPC_LOAD, nPC_LOAD, PC_DATA_IN[8], PC_DATA_IN[9], PC_DATA_IN[10], PC_DATA_IN[11], PC_DATA_IN[12], PC_DATA_IN[13], PC_DATA_IN[14], PC_DATA_IN[15], nPC_LOAD, nPC_LOAD, High_byte_p13, High_byte_p14, High_byte_p15, High_byte_p16, High_byte_p17, High_byte_p18, High_byte_p19, High_byte_p20
  // IC_74244 Low_byte_3: pin names not known; wires that end beside it: STK_DATA_IN[0], STK_DATA_IN[1], STK_DATA_IN[2], STK_DATA_IN[3], STK_DATA_IN[4], STK_DATA_IN[5], STK_DATA_IN[6], STK_DATA_IN[7], Low_byte_p9, Low_byte_p10, Low_byte_p11, Low_byte_p12, Low_byte_p13, Low_byte_p14, Low_byte_p15, Low_byte_p16
  // IC_74244 High_byte_3: pin names not known; wires that end beside it: nSTK_LOAD, nSTK_LOAD, STK_DATA_IN[8], STK_DATA_IN[9], STK_DATA_IN[10], STK_DATA_IN[11], STK_DATA_IN[12], STK_DATA_IN[13], STK_DATA_IN[14], STK_DATA_IN[15], nSTK_LOAD, nSTK_LOAD, High_byte_p13, High_byte_p14, High_byte_p15, High_byte_p16, High_byte_p17, High_byte_p18, High_byte_p19, High_byte_p20
  // IC_74377 Low_byte_4: pin names not known; wires that end beside it: Low_byte_p9, Low_byte_p10, Low_byte_p11, Low_byte_p12, Low_byte_p13, Low_byte_p14, Low_byte_p15, Low_byte_p16, DATA_OUT[0], DATA_OUT[1], DATA_OUT[2], DATA_OUT[3], DATA_OUT[4], DATA_OUT[5], DATA_OUT[6], DATA_OUT[7]
  // IC_74377 High_byte_4: pin names not known; wires that end beside it: CLOCK, nLOW_LOAD, High_byte_p13, High_byte_p14, High_byte_p15, High_byte_p16, High_byte_p17, High_byte_p18, High_byte_p19, High_byte_p20, CLOCK, nHIGH_LOAD, DATA_OUT[8], DATA_OUT[9], DATA_OUT[10], DATA_OUT[11], DATA_OUT[12], DATA_OUT[13], DATA_OUT[14], DATA_OUT[15]
  and and_1 (and_1_out, nLB_LOAD, nPC_LOAD);
  and and_2 (nLOW_LOAD, and_1_out, nSTK_LOAD);
  and and_3 (and_3_out, nHB_LOAD, nPC_LOAD);
  and and_4 (nHIGH_LOAD, and_3_out, nSTK_LOAD);

  // Notes on the sheet:
  //   Input from data bus
  //   Input from Program Counter
  //   Input from Stack Pointer
endmodule

module Memory (
  input  BOOT_ROM,
  input  PROGRAM_RAM,
  input  nRAM_LOAD,
  input  nMEM_OUT,
  input  CLOCK,
  input  [15:0] ADDRESS_IN,
  input  [7:0] DATA_IN,
  input  [7:0] MANUAL_DATA_IN,
  output [7:0] CONTENTS_OUT,
  output [7:0] DATA_OUT
);

  wire and_1_out, nMEM_OUT_t, nor_1_out, not_2_out, not_3_out, not_4_out, not_5_out, not_6_out, nRAM_CE,
       nRAM_WE, nROM_CE;

  not not_1 (nRAM_CE, nROM_CE);
  nor nor_1 (nor_1_out, ADDRESS_IN[14], ADDRESS_IN[15]);
  nand nand_1 (nROM_CE, nor_1_out, BOOT_ROM);
  not not_2 (not_2_out, nRAM_CE);
  not not_3 (not_3_out, CLOCK);
  not not_4 (not_4_out, nROM_CE);
  RAM #(.addrWidth(16)) ram_1 (
    .addr(ADDRESS_IN), .data(CONTENTS_OUT), .sel(not_2_out), .clk(not_3_out), .ld(nRAM_WE), .clr(1'b0));
  ROM #(.addrWidth(16)) rom_1 (.addr(ADDRESS_IN), .data(CONTENTS_OUT), .sel(not_4_out));
  or or_1 (nMEM_OUT_t, PROGRAM_RAM, nMEM_OUT);
  not not_5 (not_5_out, PROGRAM_RAM);
  // IC_74244 ic_74244_1: pin names not known; wires that end beside it: CONTENTS_OUT[0], CONTENTS_OUT[1], CONTENTS_OUT[2], CONTENTS_OUT[3], CONTENTS_OUT[4], CONTENTS_OUT[5], CONTENTS_OUT[6], CONTENTS_OUT[7], DATA_OUT[0], DATA_OUT[1], DATA_OUT[2], DATA_OUT[3], DATA_OUT[4], DATA_OUT[5], DATA_OUT[6], DATA_OUT[7]
  // IC_74244 ic_74244_2: pin names not known; wires that end beside it: nMEM_OUT_t, nMEM_OUT_t, DATA_IN[0], DATA_IN[1], DATA_IN[2], DATA_IN[3], DATA_IN[4], DATA_IN[5], DATA_IN[6], DATA_IN[7], CONTENTS_OUT[0], CONTENTS_OUT[1], CONTENTS_OUT[2], CONTENTS_OUT[3], CONTENTS_OUT[4], CONTENTS_OUT[5], CONTENTS_OUT[6], CONTENTS_OUT[7]
  // IC_74244 ic_74244_3: pin names not known; wires that end beside it: nRAM_LOAD, nRAM_LOAD, MANUAL_DATA_IN[0], MANUAL_DATA_IN[1], MANUAL_DATA_IN[2], MANUAL_DATA_IN[3], MANUAL_DATA_IN[4], MANUAL_DATA_IN[5], MANUAL_DATA_IN[6], MANUAL_DATA_IN[7], not_5_out, not_5_out, CONTENTS_OUT[0], CONTENTS_OUT[1], CONTENTS_OUT[2], CONTENTS_OUT[3], CONTENTS_OUT[4], CONTENTS_OUT[5], CONTENTS_OUT[6], CONTENTS_OUT[7]
  and and_1 (and_1_out, PROGRAM_RAM, CLOCK);
  not not_6 (not_6_out, nRAM_LOAD);
  nor nor_2 (nRAM_WE, and_1_out, not_6_out);

  // Notes on the sheet:
  //   Toggle output/input from/to memory chips
  //   RAM
  //   ROM
  //   contents of rom_1 (hex, n*v repeats v):
  //   e aa f bb 10 cc 11 dd 1 32760*0 bb
  //   RAM write switch
endmodule

module Clock_Divider (
  input  CLOCK,
  output CLOCK_DIV8,
  output CLOCK_DIV64
);

  wire d_ff_1_q, d_ff_1_qn, d_ff_2_q, d_ff_2_qn, d_ff_3_q, d_ff_3_qn, d_ff_4_q, d_ff_4_qn, d_ff_5_q,
       d_ff_5_qn, d_ff_6_q, d_ff_6_qn, d_ff_7_q, d_ff_7_qn;

  D_Flip_Flop d_ff_1 (.clk(CLOCK), .D(d_ff_1_qn), .Q(d_ff_1_q), .Qn(d_ff_1_qn), .en(1'b1));  // open: preset, reset
  D_Flip_Flop d_ff_2 (.clk(d_ff_1_q), .D(d_ff_2_qn), .Q(d_ff_2_q), .Qn(d_ff_2_qn), .en(1'b1));  // open: preset, reset
  D_Flip_Flop d_ff_3 (.clk(d_ff_2_q), .D(d_ff_3_qn), .Q(d_ff_3_q), .Qn(d_ff_3_qn), .en(1'b1));  // open: preset, reset
  D_Flip_Flop d_ff_4 (.clk(d_ff_3_q), .D(d_ff_4_qn), .Q(d_ff_4_q), .Qn(d_ff_4_qn), .en(1'b1));  // open: preset, reset
  not not_1 (CLOCK_DIV8, d_ff_4_q);
  D_Flip_Flop d_ff_5 (.clk(d_ff_4_q), .D(d_ff_5_qn), .Q(d_ff_5_q), .Qn(d_ff_5_qn), .en(1'b1));  // open: preset, reset
  D_Flip_Flop d_ff_6 (.clk(d_ff_5_q), .D(d_ff_6_qn), .Q(d_ff_6_q), .Qn(d_ff_6_qn), .en(1'b1));  // open: preset, reset
  D_Flip_Flop d_ff_7 (.clk(d_ff_6_q), .D(d_ff_7_qn), .Q(d_ff_7_q), .Qn(d_ff_7_qn), .en(1'b1));  // open: preset, reset
  not not_2 (CLOCK_DIV64, d_ff_7_q);
endmodule

module Temp_Control_Lines (
  input  A_DATA_OUT,
  input  A_DATA_LOAD,
  input  B_DATA_OUT,
  input  B_DATA_LOAD,
  input  C_DATA_OUT,
  input  C_DATA_LOAD,
  input  D_DATA_OUT,
  input  D_DATA_LOAD,
  input  FLAGS_LOAD,
  input  IR_LOAD,
  input  PC_INC,
  input  PC_DEC,
  input  PC_L_LOAD,
  input  PC_H_LOAD,
  input  PC_L_OUT,
  input  PC_H_OUT,
  input  STK_INC,
  input  STK_DEC,
  input  STK_RESET,
  input  ALU_A_IN,
  input  ALU_B_IN,
  input  ALU_S0,
  input  ALU_S1,
  input  ALU_S2,
  input  ALU_S3,
  input  ALU_M,
  input  ALU_Cn,
  input  ALU_OUT,
  input  MAR_LB_LOAD,
  input  MAR_HB_LOAD,
  input  MAR_PC_LOAD,
  input  MAR_STK_LOAD,
  input  MEM_BOOT_ROM,
  input  MEM_PROGRAM_ROM,
  input  MEM_RAM_LOAD,
  input  MEM_OUT
);

  wire nA_DATA_LOAD, nA_DATA_OUT, nALU_A_IN, nALU_B_IN, nALU_OUT, nB_DATA_LOAD, nB_DATA_OUT, nC_DATA_LOAD,
       nC_DATA_OUT, nD_DATA_LOAD, nD_DATA_OUT, nFLAGS_LOAD, nIR_LOAD, nMAR_HB_LOAD, nMAR_LB_LOAD,
       nMAR_PC_LOAD, nMAR_STK_LOAD, nMEM_OUT, nMEM_RAM_LOAD, nPC_H_LOAD, nPC_H_OUT, nPC_L_LOAD, nPC_L_OUT,
       nSTK_RESET;

  not not_1 (nA_DATA_OUT, A_DATA_OUT);
  not not_2 (nA_DATA_LOAD, A_DATA_LOAD);
  not not_3 (nB_DATA_OUT, B_DATA_OUT);
  not not_4 (nB_DATA_LOAD, B_DATA_LOAD);
  not not_5 (nC_DATA_OUT, C_DATA_OUT);
  not not_6 (nC_DATA_LOAD, C_DATA_LOAD);
  not not_7 (nD_DATA_OUT, D_DATA_OUT);
  not not_8 (nD_DATA_LOAD, D_DATA_LOAD);
  not not_9 (nFLAGS_LOAD, FLAGS_LOAD);
  not not_10 (nIR_LOAD, IR_LOAD);
  not not_11 (nPC_L_LOAD, PC_L_LOAD);
  not not_12 (nPC_H_LOAD, PC_H_LOAD);
  not not_13 (nPC_L_OUT, PC_L_OUT);
  not not_14 (nPC_H_OUT, PC_H_OUT);
  not not_15 (nSTK_RESET, STK_RESET);
  not not_16 (nALU_A_IN, ALU_A_IN);
  not not_17 (nALU_B_IN, ALU_B_IN);
  not not_18 (nALU_OUT, ALU_OUT);
  not not_19 (nMAR_LB_LOAD, MAR_LB_LOAD);
  not not_20 (nMAR_HB_LOAD, MAR_HB_LOAD);
  not not_21 (nMAR_PC_LOAD, MAR_PC_LOAD);
  not not_22 (nMAR_STK_LOAD, MAR_STK_LOAD);
  not not_23 (nMEM_RAM_LOAD, MEM_RAM_LOAD);
  not not_24 (nMEM_OUT, MEM_OUT);

  // Other names for the same wires on the sheet: MEM_PROGRAM_RAM = MEM_PROGRAM_ROM
endmodule

// 74161
module _74161_Clockfix (
  input  CLK,
  input  CLR,
  input  LE,
  input  CEP,
  input  CET,
  input  D1,
  input  D2,
  input  D3,
  input  D4,
  output Q1,
  output Q2,
  output Q3,
  output Q4,
  output TC
);

  wire and_1_out, and_2_out, and_3_out, and_4_out, and_5_out, and_6_out, and_7_out, and_8_out, and_9_out,
       and_10_out, and_11_out, and_12_out, not_1_out, not_2_out, or_1_out, or_2_out, or_3_out, or_4_out,
       xor_1_out, xor_2_out, xor_3_out, xor_4_out;

  not not_1 (not_1_out, CLR);
  and and_1 (and_1_out, LE, CEP, CET);
  not not_2 (not_2_out, LE);
  and and_2 (and_2_out, D1, not_2_out);
  and and_3 (and_3_out, Q1, LE);
  and and_4 (and_4_out, D2, not_2_out);
  and and_5 (and_5_out, Q2, LE);
  and and_6 (and_6_out, Q1, and_1_out);
  and and_7 (and_7_out, D3, not_2_out);
  and and_8 (and_8_out, Q3, LE);
  and and_9 (and_9_out, Q2, Q1, and_1_out);
  and and_10 (and_10_out, D4, not_2_out);
  and and_11 (and_11_out, Q4, LE);
  and and_12 (and_12_out, Q3, Q2, Q1, and_1_out);
  xor xor_1 (xor_1_out, and_3_out, and_1_out);
  xor xor_2 (xor_2_out, and_5_out, and_6_out);
  xor xor_3 (xor_3_out, and_8_out, and_9_out);
  xor xor_4 (xor_4_out, and_11_out, and_12_out);
  or or_1 (or_1_out, and_2_out, xor_1_out);
  or or_2 (or_2_out, and_4_out, xor_2_out);
  or or_3 (or_3_out, and_7_out, xor_3_out);
  or or_4 (or_4_out, and_10_out, xor_4_out);
  // D_Flip_Flop d_flip_flop_1: pin names not known; wires that end beside it: or_1_out, CLK, not_1_out, Q1
  // D_Flip_Flop d_flip_flop_2: pin names not known; wires that end beside it: or_2_out, CLK, not_1_out, Q2
  // D_Flip_Flop d_flip_flop_3: pin names not known; wires that end beside it: or_3_out, CLK, not_1_out, Q3
  // D_Flip_Flop d_flip_flop_4: pin names not known; wires that end beside it: or_4_out, CLK, not_1_out, Q4
  and and_13 (TC, Q4, Q3, Q2, Q1, CET);
endmodule
