// Logisim project TTL-Computer__.circ as structural Verilog
module Program_Counter (
);

  // _74191 74191_1: pin names not known
  // _74191 74191_2: pin names not known
  // _74191 74191_3: pin names not known
  // _74191 74191_4: pin names not known
endmodule

module Controller_Sequencer_SRtest (
  input  nOE,
  input  CE,
  input  DATA,
  input  nCLR
);

  wire dip_74161_1_p3, dip_74161_1_p4, dip_74161_1_p5, dip_74161_1_p6, dip_74595_1_p1, dip_74595_1_p3,
       dip_74595_1_p4, dip_74595_1_p5, dip_74595_1_p6, dip_74595_1_p7, dip_74595_1_p9, dip_74595_1_p10,
       dip_74595_1_p11, dip_74595_1_p12, dip_74595_1_p13, dip_74595_1_p15, dip_74595_1_p17, dip_74595_2_p1,
       dip_74595_2_p3, dip_74595_2_p5, dip_74595_2_p7, dip_74595_2_p8, dip_74595_2_p9, not_1_out;

  DotMatrix #(.matrixcols(16), .matrixrows(1), .dotshape("circle")) dotmatrix_1 (
    .col0(dip_74595_1_p1), .col1(dip_74595_1_p3), .col2(dip_74595_1_p5), .col3(dip_74595_1_p7),
    .col4(dip_74595_1_p9), .col5(dip_74595_1_p11), .col6(dip_74595_1_p13), .col7(dip_74595_1_p12),
    .col8(dip_74595_1_p15), .col9(dip_74595_1_p17), .col10(dip_74595_2_p1), .col11(dip_74595_2_p3),
    .col12(dip_74595_2_p5), .col13(dip_74595_2_p7), .col14(dip_74595_2_p9), .col15(dip_74595_2_p8));
  not not_1 (not_1_out, nCLR);
  // DIP_74595 dip_74595_1: pin names not known; wires that end beside it: dip_74595_1_p1, not_1_out, dip_74595_1_p3, dip_74595_1_p4, dip_74595_1_p5, dip_74595_1_p6, dip_74595_1_p7, nOE, dip_74595_1_p9, dip_74595_1_p10, dip_74595_1_p11, dip_74595_1_p12, dip_74595_1_p13, dip_74595_1_p10, dip_74595_1_p15, not_1_out, dip_74595_1_p17, dip_74595_1_p4
  not not_2 (dip_74595_1_p6, dip_74595_1_p4);
  Clock CLOCK (.out(dip_74595_1_p4));
  // DIP_74595 dip_74595_2: pin names not known; wires that end beside it: dip_74595_2_p1, dip_74595_1_p6, dip_74595_2_p3, nOE, dip_74595_2_p5, DATA, dip_74595_2_p7, dip_74595_2_p8, dip_74595_2_p9
  DotMatrix #(.matrixcols(4), .matrixrows(1), .dotshape("circle")) dotmatrix_2 (
    .col0(dip_74161_1_p6), .col1(dip_74161_1_p5), .col2(dip_74161_1_p4), .col3(dip_74161_1_p3));
  // DIP_74161 dip_74161_1: pin names not known; wires that end beside it: nCLR, dip_74595_1_p4, dip_74161_1_p3, dip_74161_1_p4, dip_74161_1_p5, dip_74161_1_p6, CE, CE, 1'b1
  // _74165 74165_1: pin names not known

  // Notes on the sheet:
  //   CE: pull=down
  //   DATA: pull=down
  //   nCLR: pull=down
  //   nOE: pull=down
  //   ~CLR
  //   SRCLK
  //   RCLK
endmodule
