// Logisim project 74xx-Computer.circ as structural Verilog
module _74xx_Computer (
  input  [7:0] DATA_BUS__IN,
  input  MEM_BOOT_ROM,
  input  MEM_PROGRAM_RAM,
  input  [7:0] MANUAL_DATA,
  output [7:0] DATA_BUS__OUT,
  output Fc,
  output Fz,
  output Fcmp
);

  wire ALU_M, ALU_S0, ALU_S1, ALU_S2, ALU_S3, ALU_SHR, and_1_out, CLOCK_8X, clock_divider_1_clock_div8,
       CLOCK_HALT, FLAGS_Fc_CLEAR, FLAGS_Fc_LOAD, FLAGS_Fc_SET, FLAGS_Feq_LOAD, FLAGS_Fgt_LOAD,
       FLAGS_Flt_LOAD, FLAGS_Fz_LOAD, lcd_decoder_1_lcd_clock, lcd_decoder_1_reset, MEM_BOOT_ROM_t,
       nA_DATA_LOAD, nA_DATA_OUT, nALU_AX_LOAD, nALU_AY_LOAD, nALU_OUT, nB_DATA_LOAD, nB_DATA_OUT,
       nC_DATA_LOAD, nC_DATA_OUT, nD_DATA_LOAD, nD_DATA_OUT, nIR_LOAD, nMAR_HB_LOAD, nMAR_LB_LOAD,
       nMAR_PC_LOAD, nMAR_STK_LOAD, nMAR_ZP, nMEM_OUT, nMEM_RAM_LOAD, not_2_out, not_3_out, nOUT1_LOAD,
       nOUT2_LOAD, nPC_H_LOAD, nPC_H_OUT, nPC_L_LOAD, nPC_L_OUT, nSTK_RESET, Output_tty_clock,
       Output_tty_write, PC_DEC, PC_INC, STK_DEC, STK_INC;
  wire [3:0] ALU_alu_ax_contents, ALU_alu_ax_contents_2, ALU_alu_ay_contents, ALU_alu_ay_contents_2,
       ALU_contents_bus_out, ALU_contents_bus_out_2, display_decoder_1_ram_address_out_2,
       display_decoder_1_ram_address_out_3, Memory_Access_Register_data_out_2,
       Memory_Access_Register_data_out_3, Memory_contents_out, Memory_contents_out_2,
       Program_Counter_mar_bus_out, Program_Counter_mar_bus_out_2, Program_Counter_mar_bus_out_3,
       Program_Counter_mar_bus_out_4, Register_A_contents_bus_out, Register_A_contents_bus_out_2,
       Register_B_contents_bus_out, Register_B_contents_bus_out_2, Register_C_contents_bus_out,
       Register_C_contents_bus_out_2, Register_D_contents_bus_out, Register_D_contents_bus_out_2;
  wire [4:0] ALU_fc;
  wire [6:0] lcd_decoder_1_x_coord, lcd_decoder_1_y_coord, Output_tty_data;
  wire [7:0] display_decoder_1_ram_address_out, Instruction_Register_contents_bus_out,
       Memory_Access_Register_data_out, Output_contents_bus_out;
  wire [15:0] lcd_decoder_1_color, Stack_Pointer_mar_bus_out;

  Clock clock_1 (.out(CLOCK_8X));
  not not_1 (MEM_BOOT_ROM_t, MEM_BOOT_ROM);
  Hex_Digit_Display hex_digit_display_1 (.value(DATA_BUS__IN[7:4]));  // open: dp
  Hex_Digit_Display hex_digit_display_2 (.value(DATA_BUS__IN[3:0]));  // open: dp
  Hex_Digit_Display hex_digit_display_3 (.value(Program_Counter_mar_bus_out_4));  // open: dp
  Hex_Digit_Display hex_digit_display_4 (.value(Program_Counter_mar_bus_out_3));  // open: dp
  not not_2 (not_2_out, CLOCK_HALT);
  Clock_Divider clock_divider_1 (.CLOCK(CLOCK_8X), .CLOCK_DIV8(clock_divider_1_clock_div8));  // open: CLOCK_DIV64
  Hex_Digit_Display hex_digit_display_5 (.value(Register_C_contents_bus_out_2));  // open: dp
  Hex_Digit_Display hex_digit_display_6 (.value(Register_C_contents_bus_out));  // open: dp
  Register Register_C (
    .CLOCK(and_1_out), .nDATA_OUT(nC_DATA_OUT), .nDATA_LOAD(nC_DATA_LOAD),
    .CONTENTS_BUS_OUT({Register_C_contents_bus_out_2, Register_C_contents_bus_out}),
    .DATA_BUS_OUT(DATA_BUS__IN), .DATA_BUS_IN(DATA_BUS__IN));
  Hex_Digit_Display hex_digit_display_7 (.value(Program_Counter_mar_bus_out_2));  // open: dp
  Hex_Digit_Display hex_digit_display_8 (.value(Program_Counter_mar_bus_out));  // open: dp
  Hex_Digit_Display hex_digit_display_9 (.value(Register_D_contents_bus_out));  // open: dp
  Hex_Digit_Display hex_digit_display_10 (.value(Register_D_contents_bus_out_2));  // open: dp
  Register Register_D (
    .CLOCK(and_1_out), .nDATA_OUT(nD_DATA_OUT), .nDATA_LOAD(nD_DATA_LOAD),
    .CONTENTS_BUS_OUT({Register_D_contents_bus_out_2, Register_D_contents_bus_out}),
    .DATA_BUS_OUT(DATA_BUS__IN), .DATA_BUS_IN(DATA_BUS__IN));
  Hex_Digit_Display hex_digit_display_11 (.value(Register_A_contents_bus_out));  // open: dp
  Hex_Digit_Display hex_digit_display_12 (.value(Register_A_contents_bus_out_2));  // open: dp
  Register Register_A (
    .CLOCK(and_1_out), .nDATA_OUT(nA_DATA_OUT), .nDATA_LOAD(nA_DATA_LOAD),
    .CONTENTS_BUS_OUT({Register_A_contents_bus_out_2, Register_A_contents_bus_out}),
    .DATA_BUS_OUT(DATA_BUS__IN), .DATA_BUS_IN(DATA_BUS__IN));
  Hex_Digit_Display hex_digit_display_13 (.value(Register_B_contents_bus_out));  // open: dp
  Hex_Digit_Display hex_digit_display_14 (.value(Register_B_contents_bus_out_2));  // open: dp
  Register Register_B (
    .CLOCK(and_1_out), .nDATA_OUT(nB_DATA_OUT), .nDATA_LOAD(nB_DATA_LOAD),
    .CONTENTS_BUS_OUT({Register_B_contents_bus_out_2, Register_B_contents_bus_out}),
    .DATA_BUS_OUT(DATA_BUS__IN), .DATA_BUS_IN(DATA_BUS__IN));
  and and_1 (and_1_out, not_2_out, clock_divider_1_clock_div8);
  Program_Counter Program_Counter (
    .PC_INC(PC_INC), .PC_DEC(PC_DEC), .CLOCK(and_1_out), .PC_L_DATA_IN(DATA_BUS__IN),
    .nPC_L_LOAD(nPC_L_LOAD), .PC_H_DATA_IN(DATA_BUS__IN), .nPC_H_LOAD(nPC_H_LOAD),
    .MAR_BUS_OUT({Program_Counter_mar_bus_out_4, Program_Counter_mar_bus_out_3, Program_Counter_mar_bus_out_2, Program_Counter_mar_bus_out}),
    .nPC_L_OUT(nPC_L_OUT), .PC_L_DATA_OUT(DATA_BUS__IN), .PC_H_DATA_OUT(DATA_BUS__IN), .nPC_H_OUT(nPC_H_OUT));
  not not_3 (not_3_out, Fc);
  Hex_Digit_Display hex_digit_display_15 (.value(ALU_alu_ax_contents_2));  // open: dp
  Hex_Digit_Display hex_digit_display_16 (.value(ALU_alu_ax_contents));  // open: dp
  Flags_Register Flags_Register (
    .CLOCK(and_1_out), .Fgt_IN(ALU_fc[4]), .Fz_IN(ALU_fc[1]), .Fgt_LOAD(FLAGS_Fgt_LOAD),
    .Fz_LOAD(FLAGS_Fz_LOAD), .Fcmp_OUT(Fcmp), .Flt_IN(ALU_fc[2]), .Fz_OUT(Fz), .Flt_LOAD(FLAGS_Flt_LOAD),
    .Fc_CLEAR(FLAGS_Fc_CLEAR), .Feq_IN(ALU_fc[3]), .Feq_LOAD(FLAGS_Feq_LOAD), .Fc_LOAD(FLAGS_Fc_LOAD),
    .Fc_OUT(Fc), .Fc_IN(ALU_fc[0]), .Fc_SET(FLAGS_Fc_SET));
  Hex_Digit_Display hex_digit_display_17 (.value(ALU_alu_ay_contents));  // open: dp
  Hex_Digit_Display hex_digit_display_18 (.value(ALU_alu_ay_contents_2));  // open: dp
  Hex_Digit_Display hex_digit_display_19 (.value(Stack_Pointer_mar_bus_out[15:12]));  // open: dp
  Stack_Pointer Stack_Pointer (
    .STK_DEC(STK_DEC), .CLOCK(and_1_out), .nSTK_RESET(nSTK_RESET), .MAR_BUS_OUT(Stack_Pointer_mar_bus_out),
    .STK_INC(STK_INC));
  Hex_Digit_Display hex_digit_display_20 (.value(Memory_Access_Register_data_out_3));  // open: dp
  Memory_Access_Register Memory_Access_Register (
    .LB_DATA_IN(DATA_BUS__IN), .CLOCK(and_1_out), .nLB_LOAD(nMAR_LB_LOAD), .HB_DATA_IN(DATA_BUS__IN),
    .nHB_LOAD(nMAR_HB_LOAD),
    .PC_DATA_IN({Program_Counter_mar_bus_out_4, Program_Counter_mar_bus_out_3, Program_Counter_mar_bus_out_2, Program_Counter_mar_bus_out}),
    .STK_DATA_IN(Stack_Pointer_mar_bus_out), .nPC_LOAD(nMAR_PC_LOAD), .nSTK_LOAD(nMAR_STK_LOAD),
    .DATA_OUT({Memory_Access_Register_data_out_3, Memory_Access_Register_data_out_2, Memory_Access_Register_data_out}),
    .nZP_LOAD(nMAR_ZP));
  ALU ALU (
    .DATA_BUS_IN(DATA_BUS__IN), .CLOCK(and_1_out), .nAX_IN(nALU_AX_LOAD), .nAY_IN(nALU_AY_LOAD), .S3(ALU_S3),
    .S2(ALU_S2), .S1(ALU_S1), .S0(ALU_S0), .M(ALU_M), .Cn(not_3_out), .nALU_OUT(nALU_OUT), .Flt(ALU_fc[2]),
    .Feq(ALU_fc[3]), .Fgt(ALU_fc[4]), .DATA_BUS_OUT(DATA_BUS__IN),
    .CONTENTS_BUS_OUT({ALU_contents_bus_out_2, ALU_contents_bus_out}),
    .ALU_AX_CONTENTS({ALU_alu_ax_contents_2, ALU_alu_ax_contents}),
    .ALU_AY_CONTENTS({ALU_alu_ay_contents_2, ALU_alu_ay_contents}), .SHR(ALU_SHR), .Fc(ALU_fc[0]),
    .Fz(ALU_fc[1]));
  Hex_Digit_Display hex_digit_display_21 (.value(Stack_Pointer_mar_bus_out[11:8]));  // open: dp
  Hex_Digit_Display hex_digit_display_22 (.value(Stack_Pointer_mar_bus_out[7:4]));  // open: dp
  Hex_Digit_Display hex_digit_display_23 (.value(Memory_Access_Register_data_out[7:4]));  // open: dp
  Hex_Digit_Display hex_digit_display_24 (.value(Memory_Access_Register_data_out_2));  // open: dp
  Hex_Digit_Display hex_digit_display_25 (.value(ALU_contents_bus_out_2));  // open: dp
  Hex_Digit_Display hex_digit_display_26 (.value(ALU_contents_bus_out));  // open: dp
  Hex_Digit_Display hex_digit_display_27 (.value(Stack_Pointer_mar_bus_out[3:0]));  // open: dp
  Hex_Digit_Display hex_digit_display_28 (.value(Memory_Access_Register_data_out[3:0]));  // open: dp
  Hex_Digit_Display hex_digit_display_29 (.value(Instruction_Register_contents_bus_out[7:4]));  // open: dp
  Hex_Digit_Display hex_digit_display_30 (.value(Instruction_Register_contents_bus_out[3:0]));  // open: dp
  Register Instruction_Register (
    .CLOCK(and_1_out), .nDATA_OUT(1'b0), .nDATA_LOAD(nIR_LOAD),
    .CONTENTS_BUS_OUT(Instruction_Register_contents_bus_out), .DATA_BUS_IN(DATA_BUS__IN));  // open: DATA_BUS_OUT
  Hex_Digit_Display hex_digit_display_31 (.value(Output_contents_bus_out[7:4]));  // open: dp
  Output_Control Output (
    .DATA_BUS_IN(DATA_BUS__IN), .CLOCK(and_1_out), .nOUT1_LOAD(nOUT1_LOAD),
    .CONTENTS_BUS_OUT(Output_contents_bus_out), .TTY_WRITE(Output_tty_write), .TTY_DATA(Output_tty_data),
    .TTY_CLOCK(Output_tty_clock), .CLOCK_8X(CLOCK_8X));  // open: nOUT2_LOAD
  Hex_Digit_Display hex_digit_display_32 (.value(Memory_contents_out_2));  // open: dp
  Memory Memory (
    .BOOT_ROM(MEM_BOOT_ROM_t), .PROGRAM_RAM(MEM_PROGRAM_RAM), .nRAM_LOAD(nMEM_RAM_LOAD), .nMEM_OUT(nMEM_OUT),
    .CLOCK(and_1_out), .DATA_IN(DATA_BUS__IN), .MANUAL_DATA_IN(MANUAL_DATA), .DATA_OUT(DATA_BUS__IN),
    .ADDRESS_IN({display_decoder_1_ram_address_out_3, display_decoder_1_ram_address_out_2, display_decoder_1_ram_address_out}),
    .CONTENTS_OUT({Memory_contents_out_2, Memory_contents_out}));
  Hex_Digit_Display hex_digit_display_33 (.value(Output_contents_bus_out[3:0]));  // open: dp
  Hex_Digit_Display hex_digit_display_34 (.value(Memory_contents_out));  // open: dp
  Controller Controller (
    .nA_DATA_OUT(nA_DATA_OUT), .nSTK_RESET(nSTK_RESET), .nA_DATA_LOAD(nA_DATA_LOAD),
    .nALU_AX_LOAD(nALU_AX_LOAD), .nB_DATA_OUT(nB_DATA_OUT), .nALU_AY_LOAD(nALU_AY_LOAD),
    .FLAGS_DATA_IN({Fcmp, Fz, Fc}), .nB_DATA_LOAD(nB_DATA_LOAD), .ALU_S0(ALU_S0),
    .INSTRUCTION_DATA_IN(Instruction_Register_contents_bus_out), .nC_DATA_OUT(nC_DATA_OUT), .ALU_S1(ALU_S1),
    .nC_DATA_LOAD(nC_DATA_LOAD), .ALU_S2(ALU_S2), .nD_DATA_OUT(nD_DATA_OUT), .ALU_S3(ALU_S3),
    .CLOCK(and_1_out), .nD_DATA_LOAD(nD_DATA_LOAD), .ALU_M(ALU_M), .CLOCK_8X(CLOCK_8X),
    .FLAGS_Fz_LOAD(FLAGS_Fz_LOAD), .ALU_SHR(ALU_SHR), .nIR_LOAD(nIR_LOAD), .nALU_OUT(nALU_OUT),
    .nMAR_LB_LOAD(nMAR_LB_LOAD), .PC_INC(PC_INC), .nMAR_HB_LOAD(nMAR_HB_LOAD), .nMAR_PC_LOAD(nMAR_PC_LOAD),
    .PC_DEC(PC_DEC), .nMAR_STK_LOAD(nMAR_STK_LOAD), .nPC_L_LOAD(nPC_L_LOAD), .nMEM_RAM_LOAD(nMEM_RAM_LOAD),
    .nPC_H_LOAD(nPC_H_LOAD), .nMEM_OUT(nMEM_OUT), .nPC_L_OUT(nPC_L_OUT), .nPC_H_OUT(nPC_H_OUT),
    .CLOCK_HALT(CLOCK_HALT), .STK_INC(STK_INC), .STK_DEC(STK_DEC), .FLAGS_Fc_LOAD(FLAGS_Fc_LOAD),
    .FLAGS_Flt_LOAD(FLAGS_Flt_LOAD), .FLAGS_Feq_LOAD(FLAGS_Feq_LOAD), .FLAGS_Fgt_LOAD(FLAGS_Fgt_LOAD),
    .FLAGS_Fc_CLEAR(FLAGS_Fc_CLEAR), .FLAGS_Fc_SET(FLAGS_Fc_SET), .nOUT1_LOAD(nOUT1_LOAD), .nMAR_ZP(nMAR_ZP),
    .nOUT2_LOAD(nOUT2_LOAD));
  TTY tty_1 (.data(Output_tty_data), .clk(Output_tty_clock), .we(Output_tty_write), .clr(1'b0));
  LCD_Decoder lcd_decoder_1 (
    .DATA(DATA_BUS__IN), .CLOCK(and_1_out), .nLOAD(nOUT2_LOAD), .RESET(lcd_decoder_1_reset),
    .LCD_CLOCK(lcd_decoder_1_lcd_clock), .COLOR(lcd_decoder_1_color), .X_COORD(lcd_decoder_1_x_coord),
    .Y_COORD(lcd_decoder_1_y_coord));
  Display_Decoder display_decoder_1 (
    .nMEM_RAM_LOAD(nMEM_RAM_LOAD), .nMEM_OUT(nMEM_OUT),
    .RAM_ADDRESS_IN({Memory_Access_Register_data_out_3, Memory_Access_Register_data_out_2, Memory_Access_Register_data_out}),
    .RAM_DATA_IN({Memory_contents_out_2, Memory_contents_out}),
    .RAM_ADDRESS_OUT({display_decoder_1_ram_address_out_3, display_decoder_1_ram_address_out_2, display_decoder_1_ram_address_out}),
    .CLOCK_8X(CLOCK_8X));  // open: RESET
  // LCD_Video lcd_video_1: pin names not known; wires that end beside it: lcd_decoder_1_reset, lcd_decoder_1_lcd_clock, 1'b1, lcd_decoder_1_x_coord, lcd_decoder_1_y_coord, lcd_decoder_1_color
  Hex_Digit_Display hex_digit_display_35 (.value(display_decoder_1_ram_address_out_3));  // open: dp
  Hex_Digit_Display hex_digit_display_36 (.value(display_decoder_1_ram_address_out_2));  // open: dp
  Hex_Digit_Display hex_digit_display_37 (.value(display_decoder_1_ram_address_out[3:0]));  // open: dp
  Hex_Digit_Display hex_digit_display_38 (.value(display_decoder_1_ram_address_out[7:4]));  // open: dp

  assign DATA_BUS__OUT = DATA_BUS__IN;

  // Other names for the same wires on the sheet: FLAGS_Fc = Fc

  // Notes on the sheet:
  //   AX Register
  //   AY Register
  //   ALU Result
endmodule

module Controller (
  input  [2:0] FLAGS_DATA_IN,
  input  [7:0] INSTRUCTION_DATA_IN,
  input  CLOCK,
  input  CLOCK_8X,
  output nA_DATA_OUT,
  output nSTK_RESET,
  output nA_DATA_LOAD,
  output nALU_AX_LOAD,
  output nB_DATA_OUT,
  output nALU_AY_LOAD,
  output nB_DATA_LOAD,
  output ALU_S0,
  output nC_DATA_OUT,
  output ALU_S1,
  output nC_DATA_LOAD,
  output ALU_S2,
  output nD_DATA_OUT,
  output ALU_S3,
  output nD_DATA_LOAD,
  output ALU_M,
  output FLAGS_Fz_LOAD,
  output ALU_SHR,
  output nIR_LOAD,
  output nALU_OUT,
  output nMAR_LB_LOAD,
  output PC_INC,
  output nMAR_HB_LOAD,
  output nMAR_PC_LOAD,
  output PC_DEC,
  output nMAR_STK_LOAD,
  output nPC_L_LOAD,
  output nMEM_RAM_LOAD,
  output nPC_H_LOAD,
  output nMEM_OUT,
  output nPC_L_OUT,
  output nPC_H_OUT,
  output CLOCK_HALT,
  output STK_INC,
  output FLAGS_Fc_LOAD,
  output STK_DEC,
  output FLAGS_Flt_LOAD,
  output FLAGS_Feq_LOAD,
  output FLAGS_Fgt_LOAD,
  output FLAGS_Fc_CLEAR,
  output FLAGS_Fc_SET,
  output nOUT1_LOAD,
  output nOUT2_LOAD,
  output nMAR_ZP
);

  wire A_DATA_LOAD, A_DATA_OUT, ALU_AX_LOAD, ALU_AY_LOAD, ALU_OUT, and_1_out, B_DATA_LOAD, B_DATA_OUT,
       C_DATA_LOAD, C_DATA_OUT, CLOCK_8X_out, D_DATA_LOAD, D_DATA_OUT, dip_7474_1_p1, dip_7474_1_p2,
       dip_7474_1_p3, dip_74138_1_p7, dip_74161_1_p1, ic_74377_2_p1, IN_OUT, IR_LOAD, LOAD_DONE, MAR_HB_LOAD,
       MAR_LB_LOAD, MAR_PC_LOAD, MAR_STK_LOAD, MAR_ZP, MEM_OUT, MEM_RAM_LOAD, n74161_clockfix_2_tc,
       nor_2_out, not_1_out, not_2_out, not_4_out, not_5_out, or_1_out, or_3_out, or_4_out, OUT1_LOAD,
       OUT2_LOAD, PC_H_LOAD, PC_H_OUT, PC_INC_t, PC_L_LOAD, PC_L_OUT, STK_RESET, TSTATE_0, TSTATE_1,
       TSTATE_RESET;
  wire [2:0] BANK;
  wire [3:2] undriven;
  wire [4:0] T_STATE;
  wire [5:0] ic_74377_6_p6;
  wire [7:0] ROM_DATA;

  _74161_Clockfix u_74161_clockfix_1 (
    .CLK(CLOCK), .CLR(not_1_out), .LE(1'b1), .CEP(n74161_clockfix_2_tc), .CET(n74161_clockfix_2_tc),
    .D1(1'b0), .D2(1'b0), .D3(1'b0), .D4(1'b0), .Q1(T_STATE[4]));  // open: Q2, Q3, Q4, TC
  // Probe on FLAGS_DATA_IN[2]
  Clock u_CLOCK_8X (.out(CLOCK_8X_out));
  Clock_Divider clock_divider_1 (.CLOCK(CLOCK_8X_out));  // open: CLOCK_DIV8, CLOCK_DIV64
  DotMatrix #(.matrixrows(1), .dotshape("circle")) dotmatrix_1 (
    .col0(T_STATE[4]), .col1(T_STATE[3]), .col2(T_STATE[2]), .col3(T_STATE[1]), .col4(T_STATE[0]));
  _74161_Clockfix u_74161_clockfix_2 (
    .CLK(CLOCK), .CLR(not_1_out), .LE(1'b1), .CEP(1'b1), .CET(1'b1), .D1(1'b0), .D2(1'b0), .D3(1'b0),
    .D4(1'b0), .Q1(T_STATE[0]), .Q2(T_STATE[1]), .Q3(T_STATE[2]), .Q4(T_STATE[3]), .TC(n74161_clockfix_2_tc));
  not not_1 (not_1_out, and_1_out);
  and and_1 (and_1_out, TSTATE_RESET, not_2_out);
  not not_2 (not_2_out, CLOCK);
  // Probe on FLAGS_DATA_IN[0]
  // Probe on FLAGS_DATA_IN[1]
  // Probe on INSTRUCTION_DATA_IN[5]
  // Probe on INSTRUCTION_DATA_IN[6]
  // Probe on INSTRUCTION_DATA_IN[7]
  ROM #(.addrWidth(19)) rom_1 (.addr({FLAGS_DATA_IN, INSTRUCTION_DATA_IN, T_STATE, BANK}), .data(ROM_DATA), .sel(1'b1));
  // Probe on INSTRUCTION_DATA_IN[4]
  // Probe on INSTRUCTION_DATA_IN[2]
  // Probe on INSTRUCTION_DATA_IN[3]
  nor nor_1 (TSTATE_0, T_STATE[0], T_STATE[1], T_STATE[2], T_STATE[3], T_STATE[4]);
  // Probe on INSTRUCTION_DATA_IN[1]
  // Probe on INSTRUCTION_DATA_IN[0]
  and and_2 (TSTATE_1, T_STATE[0], nor_2_out);
  nor nor_2 (nor_2_out, T_STATE[1], T_STATE[2], T_STATE[3], T_STATE[4]);
  // Probe on T_STATE[2]
  // Probe on T_STATE[4]
  // Probe on T_STATE[3]
  // Probe on T_STATE[1]
  // Probe on T_STATE[0]
  // IC_74377 ic_74377_1: pin names not known
  // DIP_7474 dip_7474_1: pin names not known; wires that end beside it: dip_7474_1_p1, dip_7474_1_p2, dip_7474_1_p3, LOAD_DONE
  not not_3 (dip_7474_1_p1, CLOCK);
  Hex_Digit_Display hex_digit_display_1 (.value({undriven, MAR_ZP, FLAGS_Fc_SET}));  // open: dp
  Hex_Digit_Display hex_digit_display_2 (.value({FLAGS_Fc_CLEAR, FLAGS_Fc_LOAD, FLAGS_Flt_LOAD, FLAGS_Feq_LOAD}));  // open: dp
  // IC_74377 ic_74377_2: pin names not known; wires that end beside it: ic_74377_2_p1
  not not_4 (not_4_out, LOAD_DONE);
  and and_3 (dip_7474_1_p3, CLOCK_8X, not_5_out);
  not not_5 (not_5_out, LOAD_DONE);
  Hex_Digit_Display hex_digit_display_3 (.value({FLAGS_Fgt_LOAD, OUT2_LOAD, OUT1_LOAD, IN_OUT}));  // open: dp
  Hex_Digit_Display hex_digit_display_4 (.value({TSTATE_RESET, CLOCK_HALT, MEM_OUT, MEM_RAM_LOAD}));  // open: dp
  // IC_74377 ic_74377_3: pin names not known; wires that end beside it: ic_74377_6_p6[5]
  and and_4 (ic_74377_2_p1, CLOCK_8X, not_4_out);
  Hex_Digit_Display hex_digit_display_5 (.value({ALU_OUT, ALU_SHR, ALU_M, ALU_S3}));  // open: dp
  Hex_Digit_Display hex_digit_display_6 (.value({MAR_STK_LOAD, MAR_PC_LOAD, MAR_HB_LOAD, MAR_LB_LOAD}));  // open: dp
  // IC_74377 ic_74377_4: pin names not known; wires that end beside it: ic_74377_2_p1, ic_74377_6_p6[4], ic_74377_2_p1, ic_74377_6_p6[3]
  Hex_Digit_Display hex_digit_display_7 (.value({ALU_S2, ALU_S1, ALU_S0, ALU_AY_LOAD}));  // open: dp
  Hex_Digit_Display hex_digit_display_8 (.value({ALU_AX_LOAD, STK_RESET, STK_DEC, STK_INC}));  // open: dp
  // IC_74377 ic_74377_5: pin names not known
  and and_5 (dip_7474_1_p2, BANK[2], BANK[1], BANK[0]);
  Hex_Digit_Display hex_digit_display_9 (.value({PC_H_OUT, PC_L_OUT, PC_H_LOAD, PC_L_LOAD}));  // open: dp
  Hex_Digit_Display hex_digit_display_10 (.value({PC_DEC, PC_INC_t, IR_LOAD, FLAGS_Fz_LOAD}));  // open: dp
  // IC_74377 ic_74377_6: pin names not known; wires that end beside it: ic_74377_2_p1, ic_74377_6_p6[2], ic_74377_2_p1, ic_74377_6_p6[1], ic_74377_2_p1, ic_74377_6_p6[0]
  // DIP_74138 dip_74138_1: pin names not known; wires that end beside it: BANK[0], ic_74377_6_p6[5], BANK[1], ic_74377_6_p6[4], BANK[2], ic_74377_6_p6[3], dip_74138_1_p7, ic_74377_6_p6[2], dip_74138_1_p7, ic_74377_6_p6[1], 1'b1, ic_74377_6_p6[0]
  // DIP_74161 dip_74161_1: pin names not known; wires that end beside it: dip_74161_1_p1, CLOCK_8X, BANK[0], 1'b0, BANK[1], 1'b0, BANK[2], 1'b0, 1'b0, 1'b1, 1'b1, 1'b1
  not not_6 (dip_74161_1_p1, LOAD_DONE);
  Hex_Digit_Display hex_digit_display_11 (.value({B_DATA_LOAD, B_DATA_OUT, A_DATA_LOAD, A_DATA_OUT}));  // open: dp
  Hex_Digit_Display hex_digit_display_12 (.value({D_DATA_LOAD, D_DATA_OUT, C_DATA_LOAD, C_DATA_OUT}));  // open: dp
  not not_7 (dip_74138_1_p7, 1'b1);
  not not_8 (nA_DATA_OUT, A_DATA_OUT);
  not not_9 (nA_DATA_LOAD, A_DATA_LOAD);
  not not_10 (nB_DATA_OUT, B_DATA_OUT);
  not not_11 (nB_DATA_LOAD, B_DATA_LOAD);
  not not_12 (nC_DATA_OUT, C_DATA_OUT);
  not not_13 (nC_DATA_LOAD, C_DATA_LOAD);
  not not_14 (nD_DATA_OUT, D_DATA_OUT);
  not not_15 (nD_DATA_LOAD, D_DATA_LOAD);
  not not_16 (nIR_LOAD, or_1_out);
  not not_17 (nPC_L_LOAD, PC_L_LOAD);
  not not_18 (nPC_H_LOAD, PC_H_LOAD);
  not not_19 (nPC_L_OUT, PC_L_OUT);
  not not_20 (nPC_H_OUT, PC_H_OUT);
  or or_1 (or_1_out, IR_LOAD, TSTATE_1);
  or or_2 (PC_INC, PC_INC_t, TSTATE_1);
  not not_21 (nSTK_RESET, STK_RESET);
  not not_22 (nALU_AX_LOAD, ALU_AX_LOAD);
  not not_23 (nALU_AY_LOAD, ALU_AY_LOAD);
  not not_24 (nALU_OUT, ALU_OUT);
  not not_25 (nMAR_LB_LOAD, MAR_LB_LOAD);
  not not_26 (nMAR_HB_LOAD, MAR_HB_LOAD);
  not not_27 (nMAR_PC_LOAD, or_3_out);
  not not_28 (nMAR_STK_LOAD, MAR_STK_LOAD);
  not not_29 (nMEM_RAM_LOAD, MEM_RAM_LOAD);
  not not_30 (nMEM_OUT, or_4_out);
  not not_31 (nOUT1_LOAD, OUT1_LOAD);
  not not_32 (nOUT2_LOAD, OUT2_LOAD);
  not not_33 (nMAR_ZP, MAR_ZP);
  or or_3 (or_3_out, MAR_PC_LOAD, TSTATE_0);
  or or_4 (or_4_out, MEM_OUT, TSTATE_1);

  // Other names for the same wires on the sheet: FLAGS[2:0] = FLAGS_DATA_IN; INSTRUCTION[7:0] = INSTRUCTION_DATA_IN

  // Notes on the sheet:
  //   T-STATE COUNTER
  //   CONTROL ROM
  //   contents of rom_1 (hex, n*v repeats v):
  //   17*0 8 255*0 4 259*0 9 0 0 0 8 251*0 21 0 0 0 8 251*0 81 0 0 0 8 251*0 6 0 0 0 8 251*0 24 0 0 0 8
  //   251*0 84 0 0 0 8 251*0 12 0 0 0 8 251*0 18 0 0 0 8 251*0 90 0 0 0 8 251*0 42 0 0 0 8 251*0 48 0 0 0
  //   8 251*0 60 0 0 0 8 248*0 40 6*0 2 0 0 4 2 0 0 0 8 240*0 40 6*0 2 0 0 4 8 0 0 0 8 240*0 40 6*0 2 0 0
  //   4 20 0 0 0 8 240*0 40 6*0 2 0 0 4 80 0 0 0 8 240*0 40 6*0 2 0 0 4 80 4*0 40 6*0 2 0 0 4 20 4*0 10 0
  //   0 10 4*0 20 0 0 40 0 0 0 2 0 0 0 2 0 0 0 8 200*0 40 6*0 2 0 0 4 80 4*0 40 6*0 2 0 0 4 20 4*0 10 0 0
  //   10 4*0 20 0 0 40 0 0 0 2 0 0 0 8 0 0 0 8 198*0 8 0 9 80 0 2 0 0 0 8 246*0 8 0 9 80 0 8 0 0 0 8 248*0
  //   40 6*0 2 0 0 4 80 4*0 40 6*0 2 0 0 4 20 4*0 10 0 0 10 4*0 20 0 0 40 0 0 0 1 0 0 0 1 0 0 0 8 200*0 40
  //   6*0 2 0 0 4 80 4*0 40 6*0 2 0 0 4 20 4*0 10 0 0 10 4*0 20 0 0 40 0 0 0 1 0 0 0 4 0 0 0 8 198*0 8 0 9
  //   80 0 20 0 0 0 8 246*0 8 0 9 80 0 80 0 0 0 8 246*0 8 7*0 4 0 9 20 1 2 0 0 0 8 238*0 8 7*0 4 0 9 20 1
  //   20 0 0 0 8 238*0 8 7*0 4 0 9 20 1 80 0 0 0 8 240*0 9 20 0 2 0 0 4 0 1 20 1 4*0 8 240*0 9 20 0 20 0 0
  //   4 0 1 20 1 4*0 8 240*0 9 20 0 80 0 0 4 0 1 20 1 4*0 8 238*0 10 7*0 4 0 8 c0 1 2 0 0 0 8 238*0 10 7*0
  //   4 0 8 c0 1 20 0 0 0 8 238*0 10 7*0 4 0 8 c0 1 80 0 0 0 8 240*0 8 c0 0 2 0 0 4 0 8 c0 1 4*0 8 240*0 8
  //   c0 0 20 0 0 4 0 8 c0 1 4*0 8 240*0 8 c0 0 80 0 0 4 0 8 c0 1 4*0 8 240*0 b 60 0 2 0 0 0 8 248*0 b 60
  //   0 20 0 0 0 8 248*0 b 60 0 80 0 0 0 8 246*0 8 0 8 20 0 2 0 0 0 8 246*0 8 0 8 20 0 20 0 0 0 8 246*0 8
  //   0 8 20 0 80 0 0 0 8 246*0 8 0 a c0 0 2 0 0 0 8 246*0 8 0 a c0 0 8 0 0 0 8 246*0 8 0 a c0 0 20 0 0 0
  //   8 246*0 8 0 a c0 0 80 0 0 0 8 248*0 a 0 0 2 0 0 0 8 248*0 a 0 0 8 0 0 0 8 248*0 a 0 0 20 0 0 0 8
  //   248*0 a 0 0 80 0 0 0 8 246*0 10 7*0 4 0 8 0 1 2 0 0 0 8 238*0 10 7*0 4 0 8 0 1 8 0 0 0 8 238*0 10
  //   7*0 4 0 8 0 1 20 0 0 0 8 238*0 10 7*0 4 0 8 0 1 80 0 0 0 8 238*0 c 0 9 e0 1 2 0 0 0 8 246*0 c 0 9 e0
  //   1 8 0 0 0 8 246*0 c 0 9 e0 1 20 0 0 0 8 246*0 c 0 9 e0 1 80 0 0 0 8 246*0 9 0 0 c0 5*0 8 248*0 40
  //   6*0 2 0 8 4 4*0 8 240*0 40 6*0 2 0 10 4 4*0 8 240*0 40 6*0 2 0 0 4 80 4*0 40 6*0 2 0 0 0 20 6*0 10
  //   10 6*0 20 40 0 0 0 8 210*0 4 7*0 4 4*0 8 7*0 2 0 0 4 20 6*0 10 10 6*0 20 40 0 0 0 8 208*0 40 6*0 2 0
  //   0 4 80 4*0 40 6*0 2 0 0 4 20 6*0 10 10 6*0 20 40 0 0 0 8 210*0 4 7*0 4 4*0 8 7*0 2 0 0 4 20 6*0 10
  //   10 6*0 20 40 0 0 0 8 208*0 40 6*0 2 0 0 4 80 4*0 40 6*0 2 0 0 4 20 6*0 10 10 6*0 20 40 0 0 0 8 210*0
  //   4 7*0 4 4*0 8 7*0 2 0 0 4 20 6*0 10 10 6*0 20 40 0 0 0 8 208*0 40 6*0 2 0 0 4 80 4*0 40 6*0 2 0 0 4
  //   20 6*0 10 10 6*0 20 40 0 0 0 8 466*0 4 7*0 4 7*0 40 20 6*0 80 80 0 0 0 1 80 1 8 40 4*0 80 6*0 1 0 1
  //   8 10 4*0 40 6*0 2 0 0 4 80 4*0 40 6*0 2 0 0 4 20 6*0 20 40 6*0 10 10 157*0 2 6*0 80 6*0 2 0 2 0 20
  //   4*0 80 6*0 2 0 0 0 80 6*0 10 10 6*0 20 40 0 0 0 8 1223*0 20 0 0 0 1 0 0 0 8 247*0 20 0 0 0 4 0 0 0 8
  //   247*0 20 0 0 0 10 0 0 0 8 247*0 20 0 0 0 40 0 0 0 8 247*0 40 0 0 0 1 0 0 0 8 247*0 40 0 0 0 4 0 0 0
  //   8 247*0 40 0 0 0 10 0 0 0 8 247*0 40 0 0 0 40 0 0 0 8 249*0 8 0 1 0 0 0 8 249*0 8 0 4 0 0 0 8 249*0
  //   8 0 10 0 0 0 8 249*0 8 0 40 0 0 0 8 249*0 10 0 1 0 0 0 8 249*0 10 0 4 0 0 0 8 249*0 10 0 10 0 0 0 8
  //   249*0 10 0 40 0 0 0 8 246*0 4 0 4 0 1 2 0 0 0 8 246*0 4 0 4 0 1 8 0 0 0 8 246*0 4 0 4 0 1 20 0 0 0 8
  //   248*0 40 6*0 2 0 0 4 20 0 0 20 0 10 0 0 10 0 0 0 1 0 0 0 1 0 0 0 8 222*0 8 7*0 4 0 9 20 1 8 0 0 0 8
  //   240*0 9 20 0 8 0 0 4 0 1 20 1 4*0 8 238*0 10 7*0 4 0 8 c0 1 8 0 0 0 8 240*0 8 c0 0 8 0 0 4 0 8 c0 1
  //   4*0 8 240*0 b 60 0 8 0 0 0 8 246*0 8 0 8 20 0 8 0 0 0 8 246*0 4 0 4 0 1 80 0 0 0 8 246*0 8 8*0 8
  //   246*0 10 8*0 8 248*0 40 6*0 2 0 0 4 80 4*0 40 6*0 2 0 0 4 20 4*0 10 0 0 10 4*0 20 0 0 40 0 0 0 2 0 8
  //   5*0 8 200*0 40 6*0 2 0 0 4 80 4*0 40 6*0 2 0 0 4 20 4*0 10 0 0 10 4*0 20 0 0 40 0 0 0 2 0 10 5*0 8
  //   456*0 10 0 0 10 4*0 20 0 0 40 0 0 0 2 0 0 0 2 0 0 0 8 232*0 10 0 0 10 4*0 20 0 0 40 0 0 0 2 0 0 0 8
  //   0 0 0 8 232*0 10 0 0 10 4*0 20 0 0 40 0 0 0 1 0 0 0 1 0 0 0 8 232*0 10 0 0 10 4*0 20 0 0 40 0 0 0 1
  //   0 0 0 4 0 0 0 8 232*0 40 6*0 2 0 0 4 80 4*0 40 6*0 2 0 0 4 20 4*0 10 0 0 10 4*0 20 0 0 40 0 0 0 2 0
  //   0 0 20 0 0 0 8 200*0 40 6*0 2 0 0 4 80 4*0 40 6*0 2 0 0 4 20 4*0 10 0 0 10 4*0 20 0 0 40 0 0 0 2 0 0
  //   0 8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
  //   CE
endmodule

module Register (
  input  [7:0] DATA_BUS_IN,
  input  CLOCK,
  input  nDATA_LOAD,
  input  nDATA_OUT,
  output [7:0] CONTENTS_BUS_OUT,
  output [7:0] DATA_BUS_OUT
);

  // IC_74377 ic_74377_1: pin names not known; wires that end beside it: CLOCK, nDATA_LOAD, CONTENTS_BUS_OUT[0], CONTENTS_BUS_OUT[1], CONTENTS_BUS_OUT[2], CONTENTS_BUS_OUT[3], CONTENTS_BUS_OUT[4], CONTENTS_BUS_OUT[5], CONTENTS_BUS_OUT[6], CONTENTS_BUS_OUT[7]
  // IC_74244 ic_74244_1: pin names not known; wires that end beside it: CONTENTS_BUS_OUT[0], CONTENTS_BUS_OUT[1], CONTENTS_BUS_OUT[2], CONTENTS_BUS_OUT[3], CONTENTS_BUS_OUT[4], CONTENTS_BUS_OUT[5], CONTENTS_BUS_OUT[6], CONTENTS_BUS_OUT[7], nDATA_OUT, nDATA_OUT, DATA_BUS_OUT[0], DATA_BUS_OUT[1], DATA_BUS_OUT[2], DATA_BUS_OUT[3], DATA_BUS_OUT[4], DATA_BUS_OUT[5], DATA_BUS_OUT[6], DATA_BUS_OUT[7]
endmodule

module Flags_Register (
  input  CLOCK,
  input  Fgt_IN,
  input  Fz_IN,
  input  Fgt_LOAD,
  input  Fz_LOAD,
  input  Flt_IN,
  input  Flt_LOAD,
  input  Fc_CLEAR,
  input  Feq_IN,
  input  Feq_LOAD,
  input  Fc_LOAD,
  input  Fc_IN,
  input  Fc_SET,
  output Fcmp_OUT,
  output Fz_OUT,
  output Fc_OUT
);

  wire and_1_out, and_2_out, and_3_out, and_4_out, and_5_out, dip_7474_1_p7, not_1_out, or_1_out, or_2_out,
       or_3_out, or_4_out;

  and and_1 (and_1_out, Fgt_IN, Fgt_LOAD);
  and and_2 (and_2_out, Flt_IN, Flt_LOAD);
  and and_3 (and_3_out, Feq_IN, Feq_LOAD);
  or or_1 (or_1_out, and_1_out, and_2_out, and_3_out);
  or or_2 (or_2_out, Fgt_LOAD, Flt_LOAD, Feq_LOAD);
  and and_4 (and_4_out, or_2_out, CLOCK);
  not not_1 (not_1_out, Fc_CLEAR);
  or or_3 (or_3_out, Fc_LOAD, Fc_SET);
  and and_5 (and_5_out, or_3_out, CLOCK);
  // DIP_7474 dip_7474_1: pin names not known; wires that end beside it: 1'b1, or_1_out, and_4_out, Fcmp_OUT, 1'b1, Fz_IN, dip_7474_1_p7, Fz_OUT
  and and_6 (dip_7474_1_p7, Fz_LOAD, CLOCK);
  or or_4 (or_4_out, Fc_IN, Fc_SET);
  // DIP_7474 dip_7474_2: pin names not known; wires that end beside it: not_1_out, or_4_out, and_5_out, Fc_OUT
endmodule

module Program_Counter (
  input  PC_INC,
  input  PC_DEC,
  input  CLOCK,
  input  [7:0] PC_L_DATA_IN,
  input  nPC_L_OUT,
  input  nPC_L_LOAD,
  input  [7:0] PC_H_DATA_IN,
  input  nPC_H_OUT,
  input  nPC_H_LOAD,
  output [7:0] PC_L_DATA_OUT,
  output [15:0] MAR_BUS_OUT,
  output [7:0] PC_H_DATA_OUT
);

  wire DOWN_nUP, n74191_1_nrco, n74191_2_nrco, n74191_3_nrco, nCLK_EN, nor_2_out;

  nor nor_1 (DOWN_nUP, PC_INC, nor_2_out);
  nor nor_2 (nor_2_out, DOWN_nUP, PC_DEC);
  nor nor_3 (nCLK_EN, PC_INC, PC_DEC);
  _74191 u_74191_1 (
    .nU_D(DOWN_nUP), .CK(CLOCK), .nCTEN(nCLK_EN), .nPL(nPC_L_LOAD), .Q0(MAR_BUS_OUT[0]), .Q1(MAR_BUS_OUT[1]),
    .Q2(MAR_BUS_OUT[2]), .Q3(MAR_BUS_OUT[3]), .D0(PC_L_DATA_IN[0]), .D1(PC_L_DATA_IN[1]),
    .D2(PC_L_DATA_IN[2]), .D3(PC_L_DATA_IN[3]), .nRCO(n74191_1_nrco));  // open: TC
  _74191 u_74191_2 (
    .nU_D(DOWN_nUP), .CK(n74191_1_nrco), .nCTEN(nCLK_EN), .nPL(nPC_L_LOAD), .Q0(MAR_BUS_OUT[4]),
    .Q1(MAR_BUS_OUT[5]), .Q2(MAR_BUS_OUT[6]), .Q3(MAR_BUS_OUT[7]), .D0(PC_L_DATA_IN[4]),
    .D1(PC_L_DATA_IN[5]), .D2(PC_L_DATA_IN[6]), .D3(PC_L_DATA_IN[7]), .nRCO(n74191_2_nrco));  // open: TC
  _74191 u_74191_3 (
    .nU_D(DOWN_nUP), .CK(n74191_2_nrco), .nCTEN(nCLK_EN), .nPL(nPC_H_LOAD), .Q0(MAR_BUS_OUT[8]),
    .Q1(MAR_BUS_OUT[9]), .Q2(MAR_BUS_OUT[10]), .Q3(MAR_BUS_OUT[11]), .D0(PC_H_DATA_IN[0]),
    .D1(PC_H_DATA_IN[1]), .D2(PC_H_DATA_IN[2]), .D3(PC_H_DATA_IN[3]), .nRCO(n74191_3_nrco));  // open: TC
  _74191 u_74191_4 (
    .nU_D(DOWN_nUP), .CK(n74191_3_nrco), .nCTEN(nCLK_EN), .nPL(nPC_H_LOAD), .Q0(MAR_BUS_OUT[12]),
    .Q1(MAR_BUS_OUT[13]), .Q2(MAR_BUS_OUT[14]), .Q3(MAR_BUS_OUT[15]), .D0(PC_H_DATA_IN[4]),
    .D1(PC_H_DATA_IN[5]), .D2(PC_H_DATA_IN[6]), .D3(PC_H_DATA_IN[7]));  // open: TC, nRCO
  // IC_74244 ic_74244_1: pin names not known; wires that end beside it: MAR_BUS_OUT[0], MAR_BUS_OUT[1], MAR_BUS_OUT[2], MAR_BUS_OUT[3], MAR_BUS_OUT[4], MAR_BUS_OUT[5], MAR_BUS_OUT[6], MAR_BUS_OUT[7], nPC_L_OUT, nPC_L_OUT, PC_L_DATA_OUT[0], PC_L_DATA_OUT[1], PC_L_DATA_OUT[2], PC_L_DATA_OUT[3], PC_L_DATA_OUT[4], PC_L_DATA_OUT[5], PC_L_DATA_OUT[6], PC_L_DATA_OUT[7]
  // IC_74244 ic_74244_2: pin names not known; wires that end beside it: MAR_BUS_OUT[8], MAR_BUS_OUT[9], MAR_BUS_OUT[10], MAR_BUS_OUT[11], MAR_BUS_OUT[12], MAR_BUS_OUT[13], MAR_BUS_OUT[14], MAR_BUS_OUT[15], nPC_H_OUT, nPC_H_OUT, PC_H_DATA_OUT[0], PC_H_DATA_OUT[1], PC_H_DATA_OUT[2], PC_H_DATA_OUT[3], PC_H_DATA_OUT[4], PC_H_DATA_OUT[5], PC_H_DATA_OUT[6], PC_H_DATA_OUT[7]
endmodule

module Stack_Pointer (
  input  STK_INC,
  input  STK_DEC,
  input  CLOCK,
  input  nSTK_RESET,
  output [15:0] MAR_BUS_OUT
);

  wire DOWN_nUP, n74191_1_nrco, nCLK_EN, nor_2_out;

  nor nor_1 (DOWN_nUP, STK_INC, nor_2_out);
  nor nor_2 (nor_2_out, DOWN_nUP, STK_DEC);
  nor nor_3 (nCLK_EN, STK_INC, STK_DEC);
  _74191 u_74191_1 (
    .nU_D(DOWN_nUP), .CK(CLOCK), .nCTEN(nCLK_EN), .nPL(nSTK_RESET), .Q0(MAR_BUS_OUT[0]), .Q1(MAR_BUS_OUT[1]),
    .Q2(MAR_BUS_OUT[2]), .Q3(MAR_BUS_OUT[3]), .D0(1'b0), .D1(1'b0), .D2(1'b0), .D3(1'b0), .nRCO(n74191_1_nrco));  // open: TC
  _74191 u_74191_2 (
    .nU_D(DOWN_nUP), .CK(n74191_1_nrco), .nCTEN(nCLK_EN), .nPL(nSTK_RESET), .Q0(MAR_BUS_OUT[4]),
    .Q1(MAR_BUS_OUT[5]), .Q2(MAR_BUS_OUT[6]), .Q3(MAR_BUS_OUT[7]), .D0(1'b0), .D1(1'b0), .D2(1'b0), .D3(1'b0));  // open: TC, nRCO

  assign MAR_BUS_OUT[15:8] = {8{1'b1}};
endmodule

module ALU (
  input  SHR,
  input  [7:0] DATA_BUS_IN,
  input  CLOCK,
  input  nAX_IN,
  input  nAY_IN,
  input  S3,
  input  S2,
  input  S1,
  input  S0,
  input  M,
  input  Cn,
  input  nALU_OUT,
  output [7:0] ALU_AX_CONTENTS,
  output [7:0] ALU_AY_CONTENTS,
  output Flt,
  output Feq,
  output Fgt,
  output [7:0] DATA_BUS_OUT,
  output [7:0] CONTENTS_BUS_OUT,
  output Fz,
  output Fc
);

  wire ALU_OUT, and_1_out, and_2_out, and_4_out, and_6_out, n74181_1_p18, n74181_1_p19, n74181_2_p18,
       n74181_2_p19, nor_1_out, nor_2_out, not_1_out, not_2_out, not_3_out, not_4_out, not_5_out, SHRz;

  not not_1 (not_1_out, SHR);
  // IC_74377 AX: pin names not known; wires that end beside it: ALU_AX_CONTENTS[0], ALU_AX_CONTENTS[1], ALU_AX_CONTENTS[2], ALU_AX_CONTENTS[3], ALU_AX_CONTENTS[4], ALU_AX_CONTENTS[5], ALU_AX_CONTENTS[6], ALU_AX_CONTENTS[7]
  // IC_74377 AY: pin names not known; wires that end beside it: CLOCK, nAX_IN, CLOCK, nAY_IN, ALU_AY_CONTENTS[0], ALU_AY_CONTENTS[1], ALU_AY_CONTENTS[2], ALU_AY_CONTENTS[3], ALU_AY_CONTENTS[4], ALU_AY_CONTENTS[5], ALU_AY_CONTENTS[6], ALU_AY_CONTENTS[7]
  // _74181 74181_1: pin names not known; wires that end beside it: ALU_AY_CONTENTS[0], ALU_AX_CONTENTS[0], S3, S2, S1, S0, Cn, M, CONTENTS_BUS_OUT[0], CONTENTS_BUS_OUT[1], CONTENTS_BUS_OUT[2], ALU_AX_CONTENTS[1], ALU_AY_CONTENTS[1], ALU_AX_CONTENTS[2], ALU_AY_CONTENTS[2], ALU_AX_CONTENTS[3], ALU_AY_CONTENTS[3], n74181_1_p18, n74181_1_p19, CONTENTS_BUS_OUT[3]
  // _74181 74181_2: pin names not known; wires that end beside it: ALU_AY_CONTENTS[4], ALU_AX_CONTENTS[4], S3, S2, S1, S0, n74181_1_p18, M, CONTENTS_BUS_OUT[4], CONTENTS_BUS_OUT[5], CONTENTS_BUS_OUT[6], ALU_AX_CONTENTS[5], ALU_AY_CONTENTS[5], ALU_AX_CONTENTS[6], ALU_AY_CONTENTS[6], ALU_AX_CONTENTS[7], ALU_AY_CONTENTS[7], n74181_2_p18, n74181_2_p19, CONTENTS_BUS_OUT[7]
  // IC_74244 ic_74244_1: pin names not known; wires that end beside it: ALU_AX_CONTENTS[1], ALU_AX_CONTENTS[2], ALU_AX_CONTENTS[3], ALU_AX_CONTENTS[4], ALU_AX_CONTENTS[5], ALU_AX_CONTENTS[6], ALU_AX_CONTENTS[7], 1'b0, not_1_out, not_1_out, DATA_BUS_OUT[0], DATA_BUS_OUT[1], DATA_BUS_OUT[2], DATA_BUS_OUT[3], DATA_BUS_OUT[4], DATA_BUS_OUT[5], DATA_BUS_OUT[6], DATA_BUS_OUT[7]
  not not_2 (not_2_out, n74181_2_p18);
  and and_1 (and_1_out, SHR, ALU_AX_CONTENTS[0]);
  and and_2 (and_2_out, n74181_1_p18, n74181_2_p18);
  or or_1 (Flt, and_2_out, n74181_2_p18);
  and and_3 (Feq, n74181_1_p19, n74181_2_p19);
  not not_3 (not_3_out, n74181_1_p18);
  not not_4 (not_4_out, n74181_2_p18);
  or or_2 (Fc, not_2_out, and_1_out);
  and and_4 (and_4_out, not_3_out, not_4_out);
  or or_3 (Fgt, and_4_out, not_4_out);
  nor nor_1 (nor_1_out, CONTENTS_BUS_OUT[0], CONTENTS_BUS_OUT[1], CONTENTS_BUS_OUT[2], CONTENTS_BUS_OUT[3], CONTENTS_BUS_OUT[4], CONTENTS_BUS_OUT[5], CONTENTS_BUS_OUT[6], CONTENTS_BUS_OUT[7]);
  nor nor_2 (nor_2_out, DATA_BUS_OUT[0], DATA_BUS_OUT[1], DATA_BUS_OUT[2], DATA_BUS_OUT[3], DATA_BUS_OUT[4], DATA_BUS_OUT[5], DATA_BUS_OUT[6], DATA_BUS_OUT[7]);
  and and_5 (SHRz, nor_2_out, SHR);
  and and_6 (and_6_out, nor_1_out, not_5_out);
  not not_5 (not_5_out, SHR);
  or or_4 (Fz, and_6_out, SHRz);
  not not_6 (ALU_OUT, nALU_OUT);
  // IC_74244 ic_74244_2: pin names not known; wires that end beside it: CONTENTS_BUS_OUT[0], CONTENTS_BUS_OUT[1], CONTENTS_BUS_OUT[2], CONTENTS_BUS_OUT[3], CONTENTS_BUS_OUT[4], CONTENTS_BUS_OUT[5], CONTENTS_BUS_OUT[6], CONTENTS_BUS_OUT[7], nALU_OUT, nALU_OUT, DATA_BUS_OUT[0], DATA_BUS_OUT[1], DATA_BUS_OUT[2], DATA_BUS_OUT[3], DATA_BUS_OUT[4], DATA_BUS_OUT[5], DATA_BUS_OUT[6], DATA_BUS_OUT[7]

  // Other names for the same wires on the sheet: SHRc = ALU_AX_CONTENTS[0]

  // Notes on the sheet:
  //   M=0   Cn=0   S=0110  (A < B)
  //   M=0   Cn=1   S=0110  (A=B)
  //   M=0   Cn=1   S=0110  (A>B)
endmodule

module Memory_Access_Register (
  input  [7:0] LB_DATA_IN,
  input  CLOCK,
  input  nLB_LOAD,
  input  [7:0] HB_DATA_IN,
  input  nHB_LOAD,
  input  [15:0] PC_DATA_IN,
  input  [15:0] STK_DATA_IN,
  input  nPC_LOAD,
  input  nSTK_LOAD,
  input  nZP_LOAD,
  output [15:0] DATA_OUT
);

  wire and_1_out, and_3_out, and_4_out, High_byte_p13, High_byte_p14, High_byte_p15, High_byte_p16,
       High_byte_p17, High_byte_p18, High_byte_p19, High_byte_p20, Low_byte_p9, Low_byte_p10, Low_byte_p11,
       Low_byte_p12, Low_byte_p13, Low_byte_p14, Low_byte_p15, Low_byte_p16, nHIGH_LOAD, nLOW_LOAD;

  // IC_74244 Low_byte: pin names not known; wires that end beside it: LB_DATA_IN[0], LB_DATA_IN[1], LB_DATA_IN[2], LB_DATA_IN[3], LB_DATA_IN[4], LB_DATA_IN[5], LB_DATA_IN[6], LB_DATA_IN[7], Low_byte_p9, Low_byte_p10, Low_byte_p11, Low_byte_p12, Low_byte_p13, Low_byte_p14, Low_byte_p15, Low_byte_p16
  // IC_74244 High_byte: pin names not known; wires that end beside it: nLB_LOAD, nLB_LOAD, HB_DATA_IN[0], HB_DATA_IN[1], HB_DATA_IN[2], HB_DATA_IN[3], HB_DATA_IN[4], HB_DATA_IN[5], HB_DATA_IN[6], HB_DATA_IN[7], nHB_LOAD, nHB_LOAD, High_byte_p13, High_byte_p14, High_byte_p15, High_byte_p16, High_byte_p17, High_byte_p18, High_byte_p19, High_byte_p20
  // IC_74244 Low_byte_2: pin names not known; wires that end beside it: PC_DATA_IN[0], PC_DATA_IN[1], PC_DATA_IN[2], PC_DATA_IN[3], PC_DATA_IN[4], PC_DATA_IN[5], PC_DATA_IN[6], PC_DATA_IN[7], Low_byte_p9, Low_byte_p10, Low_byte_p11, Low_byte_p12, Low_byte_p13, Low_byte_p14, Low_byte_p15, Low_byte_p16
  // IC_74244 High_byte_2: pin names not known; wires that end beside it: nPC_LOAD, nPC_LOAD, PC_DATA_IN[8], PC_DATA_IN[9], PC_DATA_IN[10], PC_DATA_IN[11], PC_DATA_IN[12], PC_DATA_IN[13], PC_DATA_IN[14], PC_DATA_IN[15], nPC_LOAD, High_byte_p13, High_byte_p14, High_byte_p15, High_byte_p16, High_byte_p17, High_byte_p18, High_byte_p19, High_byte_p20
  // IC_74244 High_byte_3: pin names not known; wires that end beside it: nPC_LOAD, 1'b0, 1'b1, 1'b1, 1'b1, 1'b1, 1'b1, 1'b1, 1'b1, nZP_LOAD, nZP_LOAD, High_byte_p13, High_byte_p14, High_byte_p15, High_byte_p16, High_byte_p17, High_byte_p18, High_byte_p19, High_byte_p20
  // IC_74244 Low_byte_3: pin names not known; wires that end beside it: STK_DATA_IN[0], STK_DATA_IN[1], STK_DATA_IN[2], STK_DATA_IN[3], STK_DATA_IN[4], STK_DATA_IN[5], STK_DATA_IN[6], STK_DATA_IN[7], Low_byte_p9, Low_byte_p10, Low_byte_p11, Low_byte_p12, Low_byte_p13, Low_byte_p14, Low_byte_p15, Low_byte_p16
  // IC_74244 High_byte_4: pin names not known; wires that end beside it: nSTK_LOAD, nSTK_LOAD, STK_DATA_IN[8], STK_DATA_IN[9], STK_DATA_IN[10], STK_DATA_IN[11], STK_DATA_IN[12], STK_DATA_IN[13], STK_DATA_IN[14], STK_DATA_IN[15], nSTK_LOAD, nSTK_LOAD, High_byte_p13, High_byte_p14, High_byte_p15, High_byte_p16, High_byte_p17, High_byte_p18, High_byte_p19, High_byte_p20
  // IC_74377 Low_byte_4: pin names not known; wires that end beside it: Low_byte_p9, Low_byte_p10, Low_byte_p11, Low_byte_p12, Low_byte_p13, Low_byte_p14, Low_byte_p15, Low_byte_p16, DATA_OUT[0], DATA_OUT[1], DATA_OUT[2], DATA_OUT[3], DATA_OUT[4], DATA_OUT[5], DATA_OUT[6], DATA_OUT[7]
  // IC_74377 High_byte_5: pin names not known; wires that end beside it: CLOCK, nLOW_LOAD, High_byte_p13, High_byte_p14, High_byte_p15, High_byte_p16, High_byte_p17, High_byte_p18, High_byte_p19, High_byte_p20, CLOCK, nHIGH_LOAD, DATA_OUT[8], DATA_OUT[9], DATA_OUT[10], DATA_OUT[11], DATA_OUT[12], DATA_OUT[13], DATA_OUT[14], DATA_OUT[15]
  and and_1 (and_1_out, nLB_LOAD, nPC_LOAD);
  and and_2 (nLOW_LOAD, and_1_out, nSTK_LOAD);
  and and_3 (and_3_out, nHB_LOAD, nZP_LOAD);
  and and_4 (and_4_out, and_3_out, nPC_LOAD);
  and and_5 (nHIGH_LOAD, and_4_out, nSTK_LOAD);

  // Notes on the sheet:
  //   Input from data bus
  //   Input from Program Counter
  //   Zero page offset
  //   Input from Stack Pointer
endmodule

module Memory (
  input  BOOT_ROM,
  input  PROGRAM_RAM,
  input  nRAM_LOAD,
  input  nMEM_OUT,
  input  CLOCK,
  input  [15:0] ADDRESS_IN,
  input  [7:0] DATA_IN,
  input  [7:0] MANUAL_DATA_IN,
  output [7:0] CONTENTS_OUT,
  output [7:0] DATA_OUT
);

  wire and_1_out, nMEM_OUT_t, nor_1_out, not_2_out, not_3_out, not_4_out, not_5_out, not_6_out, nRAM_CE,
       nRAM_WE, nROM_CE;

  not not_1 (nRAM_CE, nROM_CE);
  nor nor_1 (nor_1_out, ADDRESS_IN[14], ADDRESS_IN[15]);
  nand nand_1 (nROM_CE, nor_1_out, BOOT_ROM);
  not not_2 (not_2_out, nRAM_CE);
  not not_3 (not_3_out, CLOCK);
  not not_4 (not_4_out, nROM_CE);
  RAM #(.addrWidth(16)) ram_1 (
    .addr(ADDRESS_IN), .data(CONTENTS_OUT), .sel(not_2_out), .clk(not_3_out), .ld(nRAM_WE), .clr(1'b0));
  ROM #(.addrWidth(16)) rom_1 (.addr(ADDRESS_IN), .data(CONTENTS_OUT), .sel(not_4_out));
  or or_1 (nMEM_OUT_t, PROGRAM_RAM, nMEM_OUT);
  not not_5 (not_5_out, PROGRAM_RAM);
  // IC_74244 ic_74244_1: pin names not known; wires that end beside it: CONTENTS_OUT[0], CONTENTS_OUT[1], CONTENTS_OUT[2], CONTENTS_OUT[3], CONTENTS_OUT[4], CONTENTS_OUT[5], CONTENTS_OUT[6], CONTENTS_OUT[7], DATA_OUT[0], DATA_OUT[1], DATA_OUT[2], DATA_OUT[3], DATA_OUT[4], DATA_OUT[5], DATA_OUT[6], DATA_OUT[7]
  // IC_74244 ic_74244_2: pin names not known; wires that end beside it: nMEM_OUT_t, nMEM_OUT_t, DATA_IN[0], DATA_IN[1], DATA_IN[2], DATA_IN[3], DATA_IN[4], DATA_IN[5], DATA_IN[6], CONTENTS_OUT[0], CONTENTS_OUT[1], CONTENTS_OUT[2], CONTENTS_OUT[3], CONTENTS_OUT[4], CONTENTS_OUT[5], CONTENTS_OUT[6]
  // IC_74244 ic_74244_3: pin names not known; wires that end beside it: DATA_IN[7], nRAM_LOAD, nRAM_LOAD, MANUAL_DATA_IN[0], MANUAL_DATA_IN[1], MANUAL_DATA_IN[2], MANUAL_DATA_IN[3], MANUAL_DATA_IN[4], MANUAL_DATA_IN[5], MANUAL_DATA_IN[6], MANUAL_DATA_IN[7], not_5_out, not_5_out, CONTENTS_OUT[7], CONTENTS_OUT[0], CONTENTS_OUT[1], CONTENTS_OUT[2], CONTENTS_OUT[3], CONTENTS_OUT[4], CONTENTS_OUT[5], CONTENTS_OUT[6], CONTENTS_OUT[7]
  and and_1 (and_1_out, PROGRAM_RAM, CLOCK);
  not not_6 (not_6_out, nRAM_LOAD);
  nor nor_2 (nRAM_WE, and_1_out, not_6_out);

  // Notes on the sheet:
  //   Toggle output/input from/to memory chips
  //   RAM
  //   ROM
  //   contents of rom_1 (hex, n*v repeats v):
  //   e 30 60 0 e 0 60 1 73 0 3e 0 74 1 d 1c 6d 4d 73 1 34 3e 1b 3c 45 0 6 1 12260*0 48 45 4c 4c 4f 20 57
  //   4f 52 4c 44 21 20 49 27 6d 20 61 6c 69 76 65 21 21 20 3a 2d 29 20453*0 bb
  //   RAM write switch
endmodule

module Output_Control (
  input  nOUT2_LOAD,
  input  [7:0] DATA_BUS_IN,
  input  CLOCK,
  input  nOUT1_LOAD,
  input  CLOCK_8X,
  output [7:0] CONTENTS_BUS_OUT,
  output [6:0] TTY_DATA,
  output TTY_CLOCK,
  output TTY_WRITE
);

  wire dip_7474_1_p4, not_1_out, not_2_out;

  and and_1 (TTY_CLOCK, CLOCK_8X, dip_7474_1_p4);
  not not_1 (not_1_out, TTY_CLOCK);
  // IC_74377 ic_74377_1: pin names not known; wires that end beside it: nOUT2_LOAD, CLOCK, nOUT1_LOAD, CONTENTS_BUS_OUT[0], CONTENTS_BUS_OUT[1], CONTENTS_BUS_OUT[2], CONTENTS_BUS_OUT[3], CONTENTS_BUS_OUT[4], CONTENTS_BUS_OUT[5], CONTENTS_BUS_OUT[6], CONTENTS_BUS_OUT[7]
  not not_2 (not_2_out, nOUT1_LOAD);
  // DIP_7474 dip_7474_1: pin names not known; wires that end beside it: not_1_out, not_2_out, CLOCK, dip_7474_1_p4

  assign TTY_DATA = CONTENTS_BUS_OUT[6:0];
  assign TTY_WRITE = 1'b1;
endmodule

module Clock_Divider (
  input  CLOCK,
  output CLOCK_DIV8,
  output CLOCK_DIV64
);

  wire d_ff_1_q, d_ff_1_qn, d_ff_2_q, d_ff_2_qn, d_ff_3_q, d_ff_3_qn, d_ff_4_q, d_ff_4_qn, d_ff_5_q,
       d_ff_5_qn, d_ff_6_q, d_ff_6_qn, d_ff_7_q, d_ff_7_qn;

  D_Flip_Flop d_ff_1 (.clk(CLOCK), .D(d_ff_1_qn), .Q(d_ff_1_q), .Qn(d_ff_1_qn), .en(1'b1));  // open: preset, reset
  D_Flip_Flop d_ff_2 (.clk(d_ff_1_q), .D(d_ff_2_qn), .Q(d_ff_2_q), .Qn(d_ff_2_qn), .en(1'b1));  // open: preset, reset
  D_Flip_Flop d_ff_3 (.clk(d_ff_2_q), .D(d_ff_3_qn), .Q(d_ff_3_q), .Qn(d_ff_3_qn), .en(1'b1));  // open: preset, reset
  D_Flip_Flop d_ff_4 (.clk(d_ff_3_q), .D(d_ff_4_qn), .Q(d_ff_4_q), .Qn(d_ff_4_qn), .en(1'b1));  // open: preset, reset
  not not_1 (CLOCK_DIV8, d_ff_4_q);
  D_Flip_Flop d_ff_5 (.clk(d_ff_4_q), .D(d_ff_5_qn), .Q(d_ff_5_q), .Qn(d_ff_5_qn), .en(1'b1));  // open: preset, reset
  D_Flip_Flop d_ff_6 (.clk(d_ff_5_q), .D(d_ff_6_qn), .Q(d_ff_6_q), .Qn(d_ff_6_qn), .en(1'b1));  // open: preset, reset
  D_Flip_Flop d_ff_7 (.clk(d_ff_6_q), .D(d_ff_7_qn), .Q(d_ff_7_q), .Qn(d_ff_7_qn), .en(1'b1));  // open: preset, reset
  not not_2 (CLOCK_DIV64, d_ff_7_q);
endmodule

// 74161
module _74161_Clockfix (
  input  CLK,
  input  CLR,
  input  LE,
  input  CEP,
  input  CET,
  input  D1,
  input  D2,
  input  D3,
  input  D4,
  output Q1,
  output Q2,
  output Q3,
  output Q4,
  output TC
);

  wire and_1_out, and_2_out, and_3_out, and_4_out, and_5_out, and_6_out, and_7_out, and_8_out, and_9_out,
       and_10_out, and_11_out, and_12_out, not_1_out, not_2_out, or_1_out, or_2_out, or_3_out, or_4_out,
       xor_1_out, xor_2_out, xor_3_out, xor_4_out;

  not not_1 (not_1_out, CLR);
  and and_1 (and_1_out, LE, CEP, CET);
  not not_2 (not_2_out, LE);
  and and_2 (and_2_out, D1, not_2_out);
  and and_3 (and_3_out, Q1, LE);
  and and_4 (and_4_out, D2, not_2_out);
  and and_5 (and_5_out, Q2, LE);
  and and_6 (and_6_out, Q1, and_1_out);
  and and_7 (and_7_out, D3, not_2_out);
  and and_8 (and_8_out, Q3, LE);
  and and_9 (and_9_out, Q2, Q1, and_1_out);
  and and_10 (and_10_out, D4, not_2_out);
  and and_11 (and_11_out, Q4, LE);
  and and_12 (and_12_out, Q3, Q2, Q1, and_1_out);
  xor xor_1 (xor_1_out, and_3_out, and_1_out);
  xor xor_2 (xor_2_out, and_5_out, and_6_out);
  xor xor_3 (xor_3_out, and_8_out, and_9_out);
  xor xor_4 (xor_4_out, and_11_out, and_12_out);
  or or_1 (or_1_out, and_2_out, xor_1_out);
  or or_2 (or_2_out, and_4_out, xor_2_out);
  or or_3 (or_3_out, and_7_out, xor_3_out);
  or or_4 (or_4_out, and_10_out, xor_4_out);
  // D_Flip_Flop d_flip_flop_1: pin names not known; wires that end beside it: or_1_out, CLK, not_1_out, Q1
  // D_Flip_Flop d_flip_flop_2: pin names not known; wires that end beside it: or_2_out, CLK, not_1_out, Q2
  // D_Flip_Flop d_flip_flop_3: pin names not known; wires that end beside it: or_3_out, CLK, not_1_out, Q3
  // D_Flip_Flop d_flip_flop_4: pin names not known; wires that end beside it: or_4_out, CLK, not_1_out, Q4
  and and_13 (TC, Q4, Q3, Q2, Q1, CET);
endmodule

module LCD_Decoder (
  input  [7:0] DATA,
  input  CLOCK,
  input  nLOAD,
  output RESET,
  output [15:0] COLOR,
  output LCD_CLOCK,
  output [6:0] X_COORD,
  output [6:0] Y_COORD
);

  wire and_1_out, and_3_out, dip_7474_1_p4, dip_7474_1_p5, n74191_1_nrco, n74191_2_nrco, n74191_3_nrco,
       n74191_3_q3, n74191_4_q0, n74191_4_q1, nand_1_out, not_1_out, not_3_out, not_4_out, RESET_t;
  wire [7:5] ic_74377_1_p16;

  Pull_Resistor pull_resistor_1 (.node(DATA[0]));
  not not_1 (not_1_out, CLOCK);
  // IC_74377 ic_74377_1: pin names not known; wires that end beside it: DATA[0], DATA[1], DATA[2], DATA[3], DATA[4], DATA[5], DATA[6], DATA[7], not_1_out, nLOAD, COLOR[5], COLOR[6], COLOR[7], COLOR[8], COLOR[9], ic_74377_1_p16[5], ic_74377_1_p16[6], ic_74377_1_p16[7]
  and and_1 (and_1_out, ic_74377_1_p16[7], ic_74377_1_p16[6], ic_74377_1_p16[5], COLOR[9], COLOR[8], COLOR[7], COLOR[6], COLOR[5]);
  not not_2 (RESET_t, RESET);
  and and_2 (RESET, and_1_out, not_3_out);
  not not_3 (not_3_out, nLOAD);
  nand nand_1 (nand_1_out, CLOCK, nLOAD);
  and and_3 (and_3_out, CLOCK, not_3_out);
  and and_4 (LCD_CLOCK, RESET_t, dip_7474_1_p4);
  not not_4 (not_4_out, dip_7474_1_p4);
  // DIP_7474 dip_7474_1: pin names not known; wires that end beside it: nand_1_out, and_3_out, and_3_out, dip_7474_1_p4, dip_7474_1_p5
  _74191 u_74191_1 (
    .nU_D(1'b0), .CK(not_4_out), .nCTEN(1'b0), .nPL(RESET_t), .Q0(X_COORD[0]), .Q1(X_COORD[1]),
    .Q2(X_COORD[2]), .Q3(X_COORD[3]), .D0(1'b0), .D1(1'b0), .D2(1'b0), .D3(1'b0), .nRCO(n74191_1_nrco));  // open: TC
  _74191 u_74191_2 (
    .nU_D(1'b0), .CK(n74191_1_nrco), .nCTEN(1'b0), .nPL(RESET_t), .Q0(X_COORD[4]), .Q1(Y_COORD[0]),
    .Q2(Y_COORD[1]), .Q3(Y_COORD[2]), .D0(1'b0), .D1(1'b0), .D2(1'b0), .D3(1'b0), .nRCO(n74191_2_nrco));  // open: TC
  _74191 u_74191_3 (
    .nU_D(1'b0), .CK(n74191_2_nrco), .nCTEN(1'b0), .nPL(RESET_t), .Q0(Y_COORD[3]), .Q1(Y_COORD[4]),
    .Q2(dip_7474_1_p5), .Q3(n74191_3_q3), .D0(1'b0), .D1(1'b0), .D2(1'b0), .D3(1'b0), .nRCO(n74191_3_nrco));  // open: TC
  _74191 u_74191_4 (
    .nU_D(1'b0), .CK(n74191_3_nrco), .nCTEN(1'b0), .nPL(RESET_t), .Q0(n74191_4_q0), .Q1(n74191_4_q1),
    .D0(1'b0), .D1(1'b0), .D2(1'b0), .D3(1'b0));  // open: Q2, Q3, TC, nRCO

  assign {COLOR[15:10], COLOR[4:0]} = {11{1'b0}};
  assign X_COORD[6:5] = 2'b00;
  assign Y_COORD[6:5] = 2'b00;
endmodule

module Display_Decoder (
  input  nMEM_RAM_LOAD,
  input  nMEM_OUT,
  input  [15:0] RAM_ADDRESS_IN,
  input  CLOCK_8X,
  input  RESET,
  input  [7:0] RAM_DATA_IN,
  output [15:0] RAM_ADDRESS_OUT
);

  wire and_2_out, and_3_out, clock_1_out, n74191_1_nrco, n74191_2_nrco, n74191_3_nrco, nor_1_out, not_1_out,
       READ_VRAM;
  wire [13:0] VRAM_ADDRESS;

  and and_1 (READ_VRAM, nMEM_RAM_LOAD, nMEM_OUT);
  not not_1 (not_1_out, READ_VRAM);
  // IC_74244 ic_74244_1: pin names not known; wires that end beside it: RAM_ADDRESS_IN[0], RAM_ADDRESS_IN[1], RAM_ADDRESS_IN[2], RAM_ADDRESS_IN[3], RAM_ADDRESS_IN[4], RAM_ADDRESS_IN[5], RAM_ADDRESS_IN[6], RAM_ADDRESS_OUT[0], RAM_ADDRESS_OUT[1], RAM_ADDRESS_OUT[2], RAM_ADDRESS_OUT[3], RAM_ADDRESS_OUT[4], RAM_ADDRESS_OUT[5], RAM_ADDRESS_OUT[6]
  // IC_74244 ic_74244_2: pin names not known; wires that end beside it: RAM_ADDRESS_IN[7], READ_VRAM, READ_VRAM, RAM_ADDRESS_IN[8], RAM_ADDRESS_IN[9], RAM_ADDRESS_IN[10], RAM_ADDRESS_IN[11], RAM_ADDRESS_IN[12], RAM_ADDRESS_IN[13], RAM_ADDRESS_IN[14], RAM_ADDRESS_IN[15], RAM_ADDRESS_OUT[7], RAM_ADDRESS_OUT[8], RAM_ADDRESS_OUT[9], RAM_ADDRESS_OUT[10], RAM_ADDRESS_OUT[11], RAM_ADDRESS_OUT[12], RAM_ADDRESS_OUT[13], RAM_ADDRESS_OUT[14], RAM_ADDRESS_OUT[15]
  // IC_74244 ic_74244_3: pin names not known; wires that end beside it: READ_VRAM, READ_VRAM, VRAM_ADDRESS[0], VRAM_ADDRESS[1], VRAM_ADDRESS[2], VRAM_ADDRESS[3], VRAM_ADDRESS[4], VRAM_ADDRESS[5], RAM_ADDRESS_OUT[0], RAM_ADDRESS_OUT[1], RAM_ADDRESS_OUT[2], RAM_ADDRESS_OUT[3], RAM_ADDRESS_OUT[4], RAM_ADDRESS_OUT[5]
  // IC_74244 ic_74244_4: pin names not known; wires that end beside it: VRAM_ADDRESS[6], VRAM_ADDRESS[7], not_1_out, not_1_out, VRAM_ADDRESS[8], VRAM_ADDRESS[9], VRAM_ADDRESS[10], VRAM_ADDRESS[11], VRAM_ADDRESS[12], VRAM_ADDRESS[13], 1'b1, 1'b1, not_1_out, not_1_out, RAM_ADDRESS_OUT[6], RAM_ADDRESS_OUT[7], RAM_ADDRESS_OUT[8], RAM_ADDRESS_OUT[9], RAM_ADDRESS_OUT[10], RAM_ADDRESS_OUT[11], RAM_ADDRESS_OUT[12], RAM_ADDRESS_OUT[13], RAM_ADDRESS_OUT[14], RAM_ADDRESS_OUT[15], RAM_DATA_IN
  Hex_Digit_Display hex_digit_display_1 (.value(VRAM_ADDRESS[11:8]));  // open: dp
  Hex_Digit_Display hex_digit_display_2 (.value({2'b11, VRAM_ADDRESS[13:12]}));  // open: dp
  Hex_Digit_Display hex_digit_display_3 (.value(VRAM_ADDRESS[3:0]));  // open: dp
  Hex_Digit_Display hex_digit_display_4 (.value(VRAM_ADDRESS[7:4]));  // open: dp
  and and_2 (and_2_out, READ_VRAM, clock_1_out);
  Clock clock_1 (.out(clock_1_out));
  _74191 u_74191_1 (
    .nU_D(1'b0), .CK(and_2_out), .nCTEN(1'b0), .nPL(nor_1_out), .Q0(VRAM_ADDRESS[0]), .Q1(VRAM_ADDRESS[1]),
    .Q2(VRAM_ADDRESS[2]), .Q3(VRAM_ADDRESS[3]), .D0(1'b0), .D1(1'b0), .D2(1'b0), .D3(1'b0),
    .nRCO(n74191_1_nrco));  // open: TC
  _74191 u_74191_2 (
    .nU_D(1'b0), .CK(n74191_1_nrco), .nCTEN(1'b0), .nPL(nor_1_out), .Q0(VRAM_ADDRESS[4]),
    .Q1(VRAM_ADDRESS[5]), .Q2(VRAM_ADDRESS[6]), .Q3(VRAM_ADDRESS[7]), .D0(1'b0), .D1(1'b0), .D2(1'b0),
    .D3(1'b0), .nRCO(n74191_2_nrco));  // open: TC
  _74191 u_74191_3 (
    .nU_D(1'b0), .CK(n74191_2_nrco), .nCTEN(1'b0), .nPL(nor_1_out), .Q0(VRAM_ADDRESS[8]),
    .Q1(VRAM_ADDRESS[9]), .Q2(VRAM_ADDRESS[10]), .Q3(VRAM_ADDRESS[11]), .D0(1'b0), .D1(1'b1), .D2(1'b1),
    .D3(1'b1), .nRCO(n74191_3_nrco));  // open: TC
  _74191 u_74191_4 (
    .nU_D(1'b0), .CK(n74191_3_nrco), .nCTEN(1'b0), .nPL(nor_1_out), .Q0(VRAM_ADDRESS[12]),
    .Q1(VRAM_ADDRESS[13]), .D0(1'b1), .D1(1'b0), .D2(1'b1), .D3(1'b1));  // open: Q2, Q3, TC, nRCO
  and and_3 (and_3_out, VRAM_ADDRESS[8], VRAM_ADDRESS[8], VRAM_ADDRESS[9], VRAM_ADDRESS[10], VRAM_ADDRESS[11], VRAM_ADDRESS[12], VRAM_ADDRESS[13]);
  nor nor_1 (nor_1_out, and_3_out, 1'b0);
endmodule
