// Logisim project ALU-test.circ as structural Verilog: 1 circuit, main circuit main
module main (
  input  [3:0] S,
  input  [3:0] A,
  input  [3:0] B,
  input  M,
  input  Cn,
  input  [3:0] S_2,
  input  [3:0] A_2,
  input  [3:0] B_2,
  input  M_2,
  output A_B,
  output G,
  output Cn_4,
  output P,
  output A_B_2,
  output A_B_3,
  output [3:0] F,
  output G_2,
  output Cn_4_2,
  output A_B_4,
  output P_2,
  output A_B_5,
  output [3:0] F_2,
  output Cn_2
);

  // _74181 74181_1: pin names not known; wires that end beside it: B[3], A[3], B[2], A[2], B[1], A[1], B[0], A[0], M, Cn, G, Cn_2, P, F[3], F[2], A_B_2, F[1], F[0]
  // _74181 74181_2: pin names not known; wires that end beside it: B_2[3], A_2[3], B_2[2], A_2[2], B_2[1], A_2[1], B_2[0], A_2[0], M_2, Cn_2, G_2, Cn_4_2, P_2, F_2[3], F_2[2], A_B_5, F_2[1], F_2[0]
  or or_1 (A_B, Cn_2, Cn_4_2);
  and and_1 (A_B_3, A_B_2, A_B_5);
  nand nand_1 (A_B_4, Cn_2, Cn_4_2);

  assign Cn_4 = Cn_2;

  // Notes on the sheet:
  //   M=0   Cn=0   S=0110
  //   M=0   Cn=1   S=0110
  //   M=0   Cn=1   S=0110
endmodule
