// Logisim project 74191.circ as structural Verilog: 3 circuits, main circuit cascade
module cascade (
  input  nU_D,
  input  nENABLE,
  input  nPL,
  input  D0,
  input  D1,
  input  D2,
  input  D3,
  input  D4,
  input  D5,
  input  D6,
  input  D7
);

  wire CK_out, n74191_1_nrco;
  wire [3:0] n74191_1_q0, n74191_2_q0;

  Clock #(.lowDuration(4)) CK (.out(CK_out));
  _74191 u_74191_1 (
    .nU_D(nU_D), .CK(CK_out), .nCTEN(nENABLE), .nPL(nPL), .Q0(n74191_1_q0[0]), .Q1(n74191_1_q0[1]),
    .Q2(n74191_1_q0[2]), .Q3(n74191_1_q0[3]), .D0(D0), .D1(D1), .D2(D2), .D3(D3), .nRCO(n74191_1_nrco));  // open: TC
  Hex_Digit_Display hex_digit_display_1 (.value(n74191_1_q0));  // open: dp
  Hex_Digit_Display hex_digit_display_2 (.value(n74191_2_q0));  // open: dp
  _74191 u_74191_2 (
    .nU_D(nU_D), .CK(n74191_1_nrco), .nCTEN(nENABLE), .nPL(nPL), .Q0(n74191_2_q0[0]), .Q1(n74191_2_q0[1]),
    .Q2(n74191_2_q0[2]), .Q3(n74191_2_q0[3]), .D0(D4), .D1(D5), .D2(D6), .D3(D7));  // open: TC, nRCO

  // Notes on the sheet:
  //   Q outputs
  //   IC1
  //   Fig. 5.6.16 Cascaded Synchronous Counters
  //   www.learnabout-electronics.org
  //   Q outputs
  //   IC2
endmodule

module _74191 (
  input  nU_D,
  input  CK,
  input  nCTEN,
  input  nPL,
  input  D0,
  input  D1,
  input  D2,
  input  D3,
  output Q0,
  output Q1,
  output Q2,
  output Q3,
  output TC,
  output nRCO
);

  wire and_1_out, and_2_out, and_3_out, and_4_out, and_5_out, and_6_out, and_7_out, and_8_out,
       jk_flipflop_1_nq, jk_flipflop_2_nq, jk_flipflop_3_nq, nand_1_out, nand_2_out, nand_3_out, nand_4_out,
       nand_5_out, nand_6_out, nand_7_out, nand_8_out, nor_1_out, not_1_out, not_2_out, not_3_out, not_4_out,
       not_5_out, not_6_out, not_7_out, not_8_out, not_9_out, or_1_out, or_2_out, or_3_out;

  not not_1 (not_1_out, nCTEN);
  not not_2 (not_2_out, nU_D);
  JK_FlipFlop jk_flipflop_1 (
    .J(not_1_out), .CK(CK), .K(not_1_out), .nPR(nand_2_out), .nCLR(nand_1_out), .Q(Q0), .nQ(jk_flipflop_1_nq));
  nand nand_1 (nand_1_out, not_3_out, not_4_out);
  not not_3 (not_3_out, nPL);
  not not_4 (not_4_out, D0);
  not not_5 (not_5_out, nU_D);
  nand nand_2 (nand_2_out, not_3_out, D0);
  and and_1 (and_1_out, Q0, not_5_out, not_1_out);
  or or_1 (or_1_out, and_1_out, and_2_out);
  and and_2 (and_2_out, nU_D, jk_flipflop_1_nq, not_1_out);
  JK_FlipFlop jk_flipflop_2 (
    .J(or_1_out), .CK(CK), .K(or_1_out), .nPR(nand_4_out), .nCLR(nand_3_out), .Q(Q1), .nQ(jk_flipflop_2_nq));
  nand nand_3 (nand_3_out, not_3_out, not_6_out);
  nand nand_4 (nand_4_out, not_3_out, D1);
  not not_6 (not_6_out, D1);
  and and_3 (and_3_out, and_1_out, Q1, not_1_out);
  and and_4 (and_4_out, and_2_out, jk_flipflop_2_nq, not_1_out);
  or or_2 (or_2_out, and_3_out, and_4_out);
  nand nand_5 (nand_5_out, not_3_out, not_7_out);
  JK_FlipFlop jk_flipflop_3 (
    .J(or_2_out), .CK(CK), .K(or_2_out), .nPR(nand_6_out), .nCLR(nand_5_out), .Q(Q2), .nQ(jk_flipflop_3_nq));
  nand nand_6 (nand_6_out, not_3_out, D2);
  not not_7 (not_7_out, D2);
  and and_5 (and_5_out, and_3_out, Q2, not_1_out);
  and and_6 (and_6_out, and_4_out, jk_flipflop_3_nq, not_1_out);
  or or_3 (or_3_out, and_5_out, and_6_out);
  JK_FlipFlop jk_flipflop_4 (
    .J(or_3_out), .CK(CK), .K(or_3_out), .nPR(nand_8_out), .nCLR(nand_7_out), .Q(Q3));  // open: nQ
  nand nand_7 (nand_7_out, not_3_out, not_8_out);
  not not_8 (not_8_out, D3);
  not not_9 (not_9_out, CK);
  nand nand_8 (nand_8_out, not_3_out, D3);
  Hex_Digit_Display hex_digit_display_1 (.value({Q3, Q2, Q1, Q0}));  // open: dp
  nor nor_1 (nor_1_out, Q3, Q2, Q1, Q0, not_2_out);
  and and_7 (and_7_out, not_2_out, Q3, Q2, Q1, Q0);
  or or_4 (TC, nor_1_out, and_7_out);
  not not_10 (nRCO, and_8_out);
  and and_8 (and_8_out, TC, not_1_out, not_9_out);
endmodule

module JK_FlipFlop (
  input  nPR,
  input  J,
  input  CK,
  input  K,
  input  nCLR,
  output Q,
  output nQ
);

  wire not_1_out, not_2_out;

  J_K_Flip_Flop j_k_ff_1 (.J(J), .clk(CK), .K(K), .Q(Q), .Qn(nQ), .preset(not_2_out), .en(1'b1), .reset(not_1_out));
  not not_1 (not_1_out, nCLR);
  not not_2 (not_2_out, nPR);
endmodule
