// Logisim project RAM-ROM_enable.circ as structural Verilog: 1 circuit, main circuit main
module main (
  input  A14,
  input  A15,
  input  ROM_BOOT,
  output RAM_ENABLE,
  output RAM_CE,
  output L_ROM_CE,
  output L_RAM_CE
);

  wire or_1_out;

  or or_1 (or_1_out, A14, A15);
  nand nand_1 (RAM_ENABLE, or_1_out, or_1_out);
  nand nand_2 (L_ROM_CE, RAM_ENABLE, ROM_BOOT);
  nand nand_3 (L_RAM_CE, L_ROM_CE, L_ROM_CE);

  assign RAM_CE = L_ROM_CE;
endmodule
